// Logisim project CPU.circ as structural Verilog: 3 circuits, main circuit CPU
module CPU (
  input  [15:0] Instruction,
  input  Power,
  input  Sleep,
  input  Trigger,
  output [7:0] Program_Address,
  output Clock,
  output COM,
  output Write,
  output [7:0] Address,
  output [7:0] I_O
);

  wire and_1_out, and_11_out, and_12_out, and_13_out, and_14_out, and_15_out, and_16_out, and_17_out,
       and_18_out, and_19_out, and_20_out, and_21_out, and_22_out, and_23_out, and_24_out, and_25_out,
       and_26_out, and_27_out, and_28_out, and_29_out, and_30_out, and_31_out, and_32_out, and_33_out,
       and_34_out, and_37_out, and_38_out, and_39_out, and_40_out, and_41_out, and_42_out, and_43_out,
       and_44_out, and_45_out, and_46_out, and_47_out, and_48_out, and_49_out, and_50_out, and_51_out,
       and_52_out, and_53_out, and_54_out, and_55_out, and_56_out, and_57_out, and_58_out, and_59_out,
       and_60_out, and_61_out, and_62_out, and_63_out, and_64_out, and_65_out, and_66_out, and_67_out,
       and_68_out, and_69_out, and_70_out, and_71_out, and_72_out, and_73_out, and_74_out, and_75_out,
       and_76_out, and_77_out, and_78_out, and_79_out, and_80_out, and_81_out, and_82_out, and_83_out,
       and_84_out, and_85_out, and_86_out, and_87_out, and_88_out, and_89_out, and_90_out, and_91_out,
       and_92_out, and_93_out, and_94_out, and_95_out, and_96_out, and_97_out, and_98_out, and_99_out,
       and_100_out, and_101_out, and_102_out, and_103_out, and_104_out, and_105_out, and_106_out,
       and_107_out, and_108_out, and_109_out, and_110_out, and_111_out, and_112_out, and_113_out,
       and_114_out, and_115_out, and_116_out, and_117_out, and_118_out, and_119_out, and_120_out,
       and_121_out, and_122_out, and_123_out, and_124_out, and_125_out, and_126_out, and_127_out,
       and_128_out, and_129_out, and_130_out, and_131_out, and_132_out, and_133_out, and_134_out,
       and_135_out, and_136_out, and_137_out, and_138_out, and_139_out, and_140_out, and_141_out,
       and_142_out, and_143_out, and_144_out, and_145_out, and_146_out, and_147_out, and_148_out,
       and_149_out, clock_1_out, controlled_buffer_1_out, controlled_buffer_2_out, controlled_buffer_3_out,
       controlled_buffer_7_out, controlled_buffer_8_out, controlled_buffer_9_out, controlled_buffer_10_out,
       controlled_buffer_23_out, controlled_buffer_24_out, controlled_buffer_25_out,
       controlled_buffer_26_out, controlled_buffer_27_out, controlled_buffer_28_out,
       controlled_buffer_29_out, controlled_buffer_30_out, controlled_buffer_31_out,
       controlled_buffer_41_out, controlled_buffer_42_out, controlled_buffer_43_out,
       controlled_buffer_44_out, controlled_buffer_45_out, controlled_buffer_46_out,
       controlled_buffer_47_out, controlled_buffer_48_out, controlled_buffer_49_out,
       controlled_buffer_50_out, controlled_buffer_51_out, controlled_buffer_52_out,
       controlled_buffer_53_out, controlled_buffer_54_out, controlled_buffer_55_out,
       controlled_buffer_56_out, controlled_buffer_73_out, controlled_buffer_74_out,
       controlled_buffer_75_out, controlled_buffer_76_out, controlled_buffer_77_out,
       controlled_buffer_78_out, controlled_buffer_79_out, controlled_buffer_80_out,
       controlled_buffer_83_out, controlled_buffer_84_out, controlled_buffer_86_out,
       controlled_buffer_87_out, controlled_buffer_89_out, controlled_buffer_90_out,
       controlled_buffer_94_out, controlled_buffer_95_out, controlled_buffer_97_out,
       controlled_buffer_99_out, controlled_buffer_106_out, controlled_buffer_107_out,
       controlled_buffer_109_out, controlled_buffer_111_out, controlled_buffer_128_out,
       controlled_buffer_135_out, controlled_buffer_153_out, controlled_buffer_154_out,
       controlled_buffer_155_out, controlled_buffer_156_out, controlled_buffer_161_out,
       controlled_buffer_162_out, controlled_buffer_163_out, controlled_buffer_164_out,
       controlled_buffer_177_out, d_ff_9_q, d_ff_10_q, d_ff_11_q, d_ff_12_q, d_ff_13_q, d_ff_14_q, d_ff_15_q,
       d_ff_16_q, d_ff_17_q, d_ff_18_q, d_ff_19_q, d_ff_20_q, d_ff_21_q, d_ff_22_q, d_ff_23_q, d_ff_24_q,
       d_ff_25_q, d_ff_26_q, d_ff_27_q, d_ff_28_q, d_ff_29_q, d_ff_30_q, d_ff_31_q, d_ff_32_q, d_ff_33_q,
       d_ff_34_q, d_ff_35_q, d_ff_36_q, d_ff_37_q, d_ff_38_q, d_ff_39_q, d_ff_40_q, ex_out, not_1_out,
       not_2_out, not_3_out, not_4_out, not_5_out, not_6_out, not_7_out, not_8_out, not_9_out, or_1_out,
       or_2_out, or_3_out, or_4_out, or_5_out, or_6_out, or_7_out, or_8_out, or_9_out, or_10_out, or_11_out,
       or_12_out, or_13_out, or_14_out, or_15_out, or_16_out, or_17_out, or_18_out, or_19_out, or_20_out,
       or_21_out, or_22_out, or_23_out, or_24_out, or_25_out, or_26_out, or_27_out, or_28_out, or_29_out,
       or_30_out, or_31_out, or_32_out, or_33_out, or_34_out, or_35_out, or_36_out, or_37_out, or_38_out,
       or_39_out, xnor_1_out, xnor_2_out, xor_1_out, xor_2_out, xor_3_out, xor_4_out, xor_5_out, xor_6_out,
       xor_7_out, xor_8_out, xor_9_out, xor_10_out, xor_11_out, xor_12_out, xor_13_out, xor_14_out,
       xor_15_out, xor_16_out, xor_17_out, xor_18_out, xor_19_out, xor_20_out, xor_21_out, xor_22_out,
       xor_23_out, xor_24_out, xor_25_out, xor_26_out, xor_27_out, xor_28_out, xor_29_out, xor_30_out,
       xor_31_out, xor_32_out, xor_33_out, xor_34_out, xor_35_out, xor_36_out, xor_37_out, xor_38_out,
       xor_39_out, xor_40_out, xor_41_out, xor_42_out, xor_43_out, xor_44_out, xor_45_out, xor_46_out,
       xor_47_out, xor_48_out, xor_49_out, xor_50_out, xor_51_out;

  and and_1 (and_1_out, ~Sleep, clock_1_out);  // AND_Gate
  Button ex (.out(ex_out));
  not not_1 (not_1_out, Power);
  and and_2 (Clock, ~and_32_out, Power, xor_1_out);  // AND_Gate
  assign controlled_buffer_1_out = not_2_out ? xor_2_out : 1'bz;  // Controlled_Buffer controlled_buffer_1
  assign controlled_buffer_2_out = not_2_out ? not_4_out : 1'bz;  // Controlled_Buffer controlled_buffer_2
  assign controlled_buffer_3_out = not_2_out ? xor_3_out : 1'bz;  // Controlled_Buffer controlled_buffer_3
  not not_2 (not_2_out, and_31_out);
  assign controlled_buffer_3_out = and_31_out ? xor_14_out : 1'bz;  // Controlled_Buffer controlled_buffer_4
  assign controlled_buffer_1_out = and_31_out ? xor_15_out : 1'bz;  // Controlled_Buffer controlled_buffer_5
  assign controlled_buffer_2_out = and_31_out ? xor_24_out : 1'bz;  // Controlled_Buffer controlled_buffer_6
  and and_3 (Address[7], and_40_out, xor_9_out);
  and and_4 (Address[6], and_40_out, xor_10_out);
  and and_5 (Address[5], and_40_out, xor_11_out);
  and and_6 (Address[4], and_40_out, xor_12_out);
  and and_7 (Address[3], and_40_out, xor_13_out);
  and and_8 (Address[2], and_40_out, xor_14_out);
  and and_9 (Address[1], and_40_out, xor_15_out);
  and and_10 (Address[0], and_40_out, xor_24_out);
  and and_11 (and_11_out, and_40_out, Write);
  Clock clock_1 (.out(clock_1_out));
  ExactlyOne xor_1 (.out(xor_1_out), .in0(and_1_out), .in1(ex_out), .in2(Trigger));
  assign controlled_buffer_7_out = not_2_out ? xor_6_out : 1'bz;  // Controlled_Buffer controlled_buffer_7
  assign controlled_buffer_8_out = not_2_out ? xor_5_out : 1'bz;  // Controlled_Buffer controlled_buffer_8
  assign controlled_buffer_9_out = not_2_out ? xor_7_out : 1'bz;  // Controlled_Buffer controlled_buffer_9
  assign controlled_buffer_10_out = not_2_out ? xor_4_out : 1'bz;  // Controlled_Buffer controlled_buffer_10
  assign controlled_buffer_10_out = and_31_out ? xor_13_out : 1'bz;  // Controlled_Buffer controlled_buffer_11
  assign controlled_buffer_7_out = and_31_out ? xor_11_out : 1'bz;  // Controlled_Buffer controlled_buffer_12
  assign controlled_buffer_8_out = and_31_out ? xor_12_out : 1'bz;  // Controlled_Buffer controlled_buffer_13
  assign controlled_buffer_9_out = and_31_out ? xor_10_out : 1'bz;  // Controlled_Buffer controlled_buffer_14
  and and_12 (and_12_out, and_40_out, ~Write);  // AND_Gate
  not not_3 (not_3_out, Clock);
  assign I_O[7] = and_11_out ? controlled_buffer_41_out : 1'bz;  // Controlled_Buffer controlled_buffer_15
  assign I_O[6] = and_11_out ? controlled_buffer_43_out : 1'bz;  // Controlled_Buffer controlled_buffer_16
  assign I_O[5] = and_11_out ? controlled_buffer_45_out : 1'bz;  // Controlled_Buffer controlled_buffer_17
  assign I_O[4] = and_11_out ? controlled_buffer_47_out : 1'bz;  // Controlled_Buffer controlled_buffer_18
  assign I_O[3] = and_11_out ? controlled_buffer_49_out : 1'bz;  // Controlled_Buffer controlled_buffer_19
  assign I_O[2] = and_11_out ? controlled_buffer_51_out : 1'bz;  // Controlled_Buffer controlled_buffer_20
  assign I_O[1] = and_11_out ? controlled_buffer_53_out : 1'bz;  // Controlled_Buffer controlled_buffer_21
  assign I_O[0] = and_11_out ? controlled_buffer_55_out : 1'bz;  // Controlled_Buffer controlled_buffer_22
  assign controlled_buffer_23_out = and_12_out ? I_O[7] : 1'bz;  // Controlled_Buffer controlled_buffer_23
  assign controlled_buffer_24_out = and_12_out ? I_O[6] : 1'bz;  // Controlled_Buffer controlled_buffer_24
  assign controlled_buffer_25_out = and_12_out ? I_O[5] : 1'bz;  // Controlled_Buffer controlled_buffer_25
  assign controlled_buffer_26_out = and_12_out ? I_O[4] : 1'bz;  // Controlled_Buffer controlled_buffer_26
  assign controlled_buffer_27_out = and_12_out ? I_O[3] : 1'bz;  // Controlled_Buffer controlled_buffer_27
  assign controlled_buffer_28_out = and_12_out ? I_O[2] : 1'bz;  // Controlled_Buffer controlled_buffer_28
  assign controlled_buffer_29_out = and_12_out ? I_O[1] : 1'bz;  // Controlled_Buffer controlled_buffer_29
  assign controlled_buffer_30_out = and_12_out ? I_O[0] : 1'bz;  // Controlled_Buffer controlled_buffer_30
  not not_4 (not_4_out, Program_Address[0]);
  xor xor_2 (xor_2_out, Program_Address[0], Program_Address[1]);
  and and_13 (and_13_out, Program_Address[1], Program_Address[0]);
  xor xor_3 (xor_3_out, and_13_out, Program_Address[2]);
  and and_14 (and_14_out, Program_Address[2], and_13_out);
  xor xor_4 (xor_4_out, and_14_out, Program_Address[3]);
  and and_15 (and_15_out, Program_Address[3], and_14_out);
  xor xor_5 (xor_5_out, and_15_out, Program_Address[4]);
  and and_16 (and_16_out, Program_Address[4], and_15_out);
  xor xor_6 (xor_6_out, and_16_out, Program_Address[5]);
  and and_17 (and_17_out, Program_Address[5], and_16_out);
  xor xor_7 (xor_7_out, and_17_out, Program_Address[6]);
  and and_18 (and_18_out, Program_Address[6], and_17_out);
  xor xor_8 (xor_8_out, and_18_out, Program_Address[7]);
  D_Flip_Flop d_ff_1 (
    .clk(Clock), .D(controlled_buffer_31_out), .Q(Program_Address[7]), .reset(not_1_out));  // open: Qn, preset, en
  assign controlled_buffer_31_out = not_2_out ? xor_8_out : 1'bz;  // Controlled_Buffer controlled_buffer_31
  D_Flip_Flop d_ff_2 (
    .clk(Clock), .D(controlled_buffer_9_out), .Q(Program_Address[6]), .reset(not_1_out));  // open: Qn, preset, en
  D_Flip_Flop d_ff_3 (
    .clk(Clock), .D(controlled_buffer_7_out), .Q(Program_Address[5]), .reset(not_1_out));  // open: Qn, preset, en
  D_Flip_Flop d_ff_4 (
    .clk(Clock), .D(controlled_buffer_8_out), .Q(Program_Address[4]), .reset(not_1_out));  // open: Qn, preset, en
  D_Flip_Flop d_ff_5 (
    .clk(Clock), .D(controlled_buffer_10_out), .Q(Program_Address[3]), .reset(not_1_out));  // open: Qn, preset, en
  D_Flip_Flop d_ff_6 (
    .clk(Clock), .D(controlled_buffer_3_out), .Q(Program_Address[2]), .reset(not_1_out));  // open: Qn, preset, en
  D_Flip_Flop d_ff_7 (
    .clk(Clock), .D(controlled_buffer_1_out), .Q(Program_Address[1]), .reset(not_1_out));  // open: Qn, preset, en
  D_Flip_Flop d_ff_8 (
    .clk(Clock), .D(controlled_buffer_2_out), .Q(Program_Address[0]), .reset(not_1_out));  // open: Qn, preset, en
  assign controlled_buffer_31_out = and_31_out ? xor_9_out : 1'bz;  // Controlled_Buffer controlled_buffer_32
  assign controlled_buffer_30_out = and_33_out ? Program_Address[7] : 1'bz;  // Controlled_Buffer controlled_buffer_33
  and and_19 (and_19_out, Instruction[8], not_3_out, Instruction[9]);
  and and_20 (and_20_out, ~Instruction[8], not_3_out, Instruction[9]);  // AND_Gate
  and and_21 (and_21_out, Instruction[8], not_3_out, ~Instruction[9]);  // AND_Gate
  and and_22 (and_22_out, ~Instruction[8], not_3_out, ~Instruction[9]);  // AND_Gate
  and and_23 (and_23_out, Instruction[8], Instruction[9]);
  and and_24 (and_24_out, ~Instruction[8], Instruction[9]);  // AND_Gate
  and and_25 (and_25_out, Instruction[8], ~Instruction[9]);  // AND_Gate
  and and_26 (and_26_out, ~Instruction[8], ~Instruction[9]);  // AND_Gate
  and and_27 (and_27_out, Instruction[10], Instruction[11]);
  and and_28 (and_28_out, ~Instruction[10], Instruction[11]);  // AND_Gate
  and and_29 (and_29_out, Instruction[10], ~Instruction[11]);  // AND_Gate
  and and_30 (and_30_out, ~Instruction[10], ~Instruction[11]);  // AND_Gate
  assign controlled_buffer_29_out = and_33_out ? Program_Address[6] : 1'bz;  // Controlled_Buffer controlled_buffer_34
  assign controlled_buffer_27_out = and_33_out ? Program_Address[4] : 1'bz;  // Controlled_Buffer controlled_buffer_35
  assign controlled_buffer_28_out = and_33_out ? Program_Address[5] : 1'bz;  // Controlled_Buffer controlled_buffer_36
  assign controlled_buffer_26_out = and_33_out ? Program_Address[3] : 1'bz;  // Controlled_Buffer controlled_buffer_37
  and and_31 (and_31_out, ~xor_46_out, and_41_out);  // AND_Gate
  assign controlled_buffer_25_out = and_33_out ? Program_Address[2] : 1'bz;  // Controlled_Buffer controlled_buffer_38
  assign controlled_buffer_24_out = and_33_out ? Program_Address[1] : 1'bz;  // Controlled_Buffer controlled_buffer_39
  assign controlled_buffer_23_out = and_33_out ? Program_Address[0] : 1'bz;  // Controlled_Buffer controlled_buffer_40
  D_Flip_Flop d_ff_9 (
    .clk(and_21_out), .D(controlled_buffer_23_out), .Q(d_ff_9_q), .reset(not_1_out));  // open: Qn, preset, en
  D_Flip_Flop d_ff_10 (
    .clk(and_21_out), .D(controlled_buffer_24_out), .Q(d_ff_10_q), .reset(not_1_out));  // open: Qn, preset, en
  D_Flip_Flop d_ff_11 (
    .clk(and_21_out), .D(controlled_buffer_25_out), .Q(d_ff_11_q), .reset(not_1_out));  // open: Qn, preset, en
  D_Flip_Flop d_ff_12 (
    .clk(and_21_out), .D(controlled_buffer_26_out), .Q(d_ff_12_q), .reset(not_1_out));  // open: Qn, preset, en
  D_Flip_Flop d_ff_13 (
    .clk(and_21_out), .D(controlled_buffer_27_out), .Q(d_ff_13_q), .reset(not_1_out));  // open: Qn, preset, en
  D_Flip_Flop d_ff_14 (
    .clk(and_21_out), .D(controlled_buffer_28_out), .Q(d_ff_14_q), .reset(not_1_out));  // open: Qn, preset, en
  D_Flip_Flop d_ff_15 (
    .clk(and_21_out), .D(controlled_buffer_29_out), .Q(d_ff_15_q), .reset(not_1_out));  // open: Qn, preset, en
  D_Flip_Flop d_ff_16 (
    .clk(and_21_out), .D(controlled_buffer_30_out), .Q(d_ff_16_q), .reset(not_1_out));  // open: Qn, preset, en
  D_Flip_Flop d_ff_17 (
    .clk(and_22_out), .D(controlled_buffer_23_out), .Q(d_ff_17_q), .reset(not_1_out));  // open: Qn, preset, en
  D_Flip_Flop d_ff_18 (
    .clk(and_22_out), .D(controlled_buffer_24_out), .Q(d_ff_18_q), .reset(not_1_out));  // open: Qn, preset, en
  D_Flip_Flop d_ff_19 (
    .clk(and_22_out), .D(controlled_buffer_25_out), .Q(d_ff_19_q), .reset(not_1_out));  // open: Qn, preset, en
  D_Flip_Flop d_ff_20 (
    .clk(and_22_out), .D(controlled_buffer_26_out), .Q(d_ff_20_q), .reset(not_1_out));  // open: Qn, preset, en
  D_Flip_Flop d_ff_21 (
    .clk(and_22_out), .D(controlled_buffer_27_out), .Q(d_ff_21_q), .reset(not_1_out));  // open: Qn, preset, en
  D_Flip_Flop d_ff_22 (
    .clk(and_22_out), .D(controlled_buffer_28_out), .Q(d_ff_22_q), .reset(not_1_out));  // open: Qn, preset, en
  D_Flip_Flop d_ff_23 (
    .clk(and_22_out), .D(controlled_buffer_29_out), .Q(d_ff_23_q), .reset(not_1_out));  // open: Qn, preset, en
  D_Flip_Flop d_ff_24 (
    .clk(and_22_out), .D(controlled_buffer_30_out), .Q(d_ff_24_q), .reset(not_1_out));  // open: Qn, preset, en
  and and_32 (and_32_out, Instruction[15], Instruction[14], Instruction[13], Instruction[12]);
  and and_33 (and_33_out, Instruction[10], and_41_out);
  and and_34 (and_34_out, Instruction[11], ~and_42_out);  // AND_Gate
  and and_35 (COM, and_40_out, Instruction[13]);
  and and_36 (Write, and_40_out, Instruction[12]);
  xor xor_9 (xor_9_out, controlled_buffer_73_out, xor_17_out);
  xor xor_10 (xor_10_out, controlled_buffer_74_out, xor_18_out);
  xor xor_11 (xor_11_out, controlled_buffer_79_out, xor_19_out);
  xor xor_12 (xor_12_out, controlled_buffer_77_out, xor_20_out);
  xor xor_13 (xor_13_out, controlled_buffer_78_out, xor_21_out);
  xor xor_14 (xor_14_out, controlled_buffer_80_out, xor_22_out);
  xor xor_15 (xor_15_out, controlled_buffer_89_out, xor_23_out);
  assign controlled_buffer_41_out = and_25_out ? d_ff_9_q : 1'bz;  // Controlled_Buffer controlled_buffer_41
  assign controlled_buffer_42_out = and_29_out ? d_ff_9_q : 1'bz;  // Controlled_Buffer controlled_buffer_42
  assign controlled_buffer_43_out = and_25_out ? d_ff_10_q : 1'bz;  // Controlled_Buffer controlled_buffer_43
  assign controlled_buffer_44_out = and_29_out ? d_ff_10_q : 1'bz;  // Controlled_Buffer controlled_buffer_44
  assign controlled_buffer_45_out = and_25_out ? d_ff_11_q : 1'bz;  // Controlled_Buffer controlled_buffer_45
  assign controlled_buffer_46_out = and_29_out ? d_ff_11_q : 1'bz;  // Controlled_Buffer controlled_buffer_46
  assign controlled_buffer_47_out = and_25_out ? d_ff_12_q : 1'bz;  // Controlled_Buffer controlled_buffer_47
  assign controlled_buffer_48_out = and_29_out ? d_ff_12_q : 1'bz;  // Controlled_Buffer controlled_buffer_48
  assign controlled_buffer_49_out = and_25_out ? d_ff_13_q : 1'bz;  // Controlled_Buffer controlled_buffer_49
  assign controlled_buffer_50_out = and_29_out ? d_ff_13_q : 1'bz;  // Controlled_Buffer controlled_buffer_50
  assign controlled_buffer_51_out = and_25_out ? d_ff_14_q : 1'bz;  // Controlled_Buffer controlled_buffer_51
  assign controlled_buffer_52_out = and_29_out ? d_ff_14_q : 1'bz;  // Controlled_Buffer controlled_buffer_52
  assign controlled_buffer_53_out = and_25_out ? d_ff_15_q : 1'bz;  // Controlled_Buffer controlled_buffer_53
  assign controlled_buffer_54_out = and_29_out ? d_ff_15_q : 1'bz;  // Controlled_Buffer controlled_buffer_54
  assign controlled_buffer_55_out = and_25_out ? d_ff_16_q : 1'bz;  // Controlled_Buffer controlled_buffer_55
  assign controlled_buffer_56_out = and_29_out ? d_ff_16_q : 1'bz;  // Controlled_Buffer controlled_buffer_56
  assign controlled_buffer_41_out = and_26_out ? d_ff_17_q : 1'bz;  // Controlled_Buffer controlled_buffer_57
  assign controlled_buffer_42_out = and_30_out ? d_ff_17_q : 1'bz;  // Controlled_Buffer controlled_buffer_58
  assign controlled_buffer_43_out = and_26_out ? d_ff_18_q : 1'bz;  // Controlled_Buffer controlled_buffer_59
  assign controlled_buffer_44_out = and_30_out ? d_ff_18_q : 1'bz;  // Controlled_Buffer controlled_buffer_60
  assign controlled_buffer_45_out = and_26_out ? d_ff_19_q : 1'bz;  // Controlled_Buffer controlled_buffer_61
  assign controlled_buffer_46_out = and_30_out ? d_ff_19_q : 1'bz;  // Controlled_Buffer controlled_buffer_62
  assign controlled_buffer_47_out = and_26_out ? d_ff_20_q : 1'bz;  // Controlled_Buffer controlled_buffer_63
  assign controlled_buffer_48_out = and_30_out ? d_ff_20_q : 1'bz;  // Controlled_Buffer controlled_buffer_64
  assign controlled_buffer_49_out = and_26_out ? d_ff_21_q : 1'bz;  // Controlled_Buffer controlled_buffer_65
  assign controlled_buffer_50_out = and_30_out ? d_ff_21_q : 1'bz;  // Controlled_Buffer controlled_buffer_66
  assign controlled_buffer_51_out = and_26_out ? d_ff_22_q : 1'bz;  // Controlled_Buffer controlled_buffer_67
  assign controlled_buffer_52_out = and_30_out ? d_ff_22_q : 1'bz;  // Controlled_Buffer controlled_buffer_68
  assign controlled_buffer_53_out = and_26_out ? d_ff_23_q : 1'bz;  // Controlled_Buffer controlled_buffer_69
  assign controlled_buffer_54_out = and_30_out ? d_ff_23_q : 1'bz;  // Controlled_Buffer controlled_buffer_70
  assign controlled_buffer_55_out = and_26_out ? d_ff_24_q : 1'bz;  // Controlled_Buffer controlled_buffer_71
  assign controlled_buffer_56_out = and_30_out ? d_ff_24_q : 1'bz;  // Controlled_Buffer controlled_buffer_72
  and and_37 (and_37_out, Instruction[10], Instruction[13]);
  and and_38 (and_38_out, Instruction[11], Instruction[10], Instruction[12]);
  and and_39 (and_39_out, ~Instruction[11], ~Instruction[10], Instruction[12]);  // AND_Gate
  xor xor_16 (xor_16_out, Instruction[12], Instruction[13]);
  and and_40 (and_40_out, Instruction[15], ~Instruction[14]);  // AND_Gate
  and and_41 (and_41_out, ~Instruction[15], Instruction[14]);  // AND_Gate
  and and_42 (and_42_out, ~Instruction[13], and_41_out);  // AND_Gate
  and and_43 (and_43_out, Instruction[12], Instruction[13]);
  and and_44 (and_44_out, ~and_43_out, and_41_out);  // AND_Gate
  xor xor_17 (xor_17_out, controlled_buffer_75_out, or_1_out);
  or or_1 (or_1_out, and_45_out, and_46_out);
  and and_45 (and_45_out, xor_18_out, controlled_buffer_74_out);
  and and_46 (and_46_out, controlled_buffer_83_out, or_2_out);
  xor xor_18 (xor_18_out, controlled_buffer_83_out, or_2_out);
  or or_2 (or_2_out, and_48_out, and_47_out);
  and and_47 (and_47_out, controlled_buffer_84_out, or_3_out);
  and and_48 (and_48_out, xor_19_out, controlled_buffer_79_out);
  xor xor_19 (xor_19_out, controlled_buffer_84_out, or_3_out);
  or or_3 (or_3_out, and_50_out, and_49_out);
  and and_49 (and_49_out, controlled_buffer_95_out, or_4_out);
  and and_50 (and_50_out, xor_20_out, controlled_buffer_77_out);
  xor xor_20 (xor_20_out, controlled_buffer_95_out, or_4_out);
  or or_4 (or_4_out, and_51_out, and_52_out);
  and and_51 (and_51_out, xor_21_out, controlled_buffer_78_out);
  and and_52 (and_52_out, controlled_buffer_94_out, or_5_out);
  xor xor_21 (xor_21_out, controlled_buffer_94_out, or_5_out);
  or or_5 (or_5_out, and_54_out, and_53_out);
  and and_53 (and_53_out, controlled_buffer_106_out, or_6_out);
  and and_54 (and_54_out, xor_22_out, controlled_buffer_80_out);
  xor xor_22 (xor_22_out, controlled_buffer_106_out, or_6_out);
  or or_6 (or_6_out, and_55_out, and_56_out);
  and and_55 (and_55_out, xor_23_out, controlled_buffer_89_out);
  and and_56 (and_56_out, controlled_buffer_107_out, and_57_out);
  xor xor_23 (xor_23_out, controlled_buffer_107_out, and_57_out);
  and and_57 (and_57_out, controlled_buffer_90_out, controlled_buffer_128_out);
  xor xor_24 (xor_24_out, controlled_buffer_90_out, controlled_buffer_128_out);
  and and_58 (and_58_out, Instruction[15], Instruction[14], ~Instruction[13], ~Instruction[12]);  // AND_Gate
  or or_7 (or_7_out, and_37_out, and_38_out, and_39_out);
  and and_59 (and_59_out, or_7_out, and_62_out);
  and and_60 (and_60_out, Instruction[11], and_62_out);
  and and_61 (and_61_out, Instruction[13], and_62_out);
  and and_62 (and_62_out, xor_16_out, ~Instruction[15], ~Instruction[14]);  // AND_Gate
  xnor xnor_1 (xnor_1_out, Instruction[15], Instruction[14]);
  and and_63 (and_63_out, and_41_out, Instruction[13], Instruction[12]);
  assign controlled_buffer_73_out = and_44_out ? Program_Address[7] : 1'bz;  // Controlled_Buffer controlled_buffer_73
  assign controlled_buffer_74_out = and_44_out ? Program_Address[6] : 1'bz;  // Controlled_Buffer controlled_buffer_74
  and and_64 (and_64_out, and_44_out, and_34_out);
  and and_65 (and_65_out, ~and_34_out, and_63_out);  // AND_Gate
  or or_8 (or_8_out, and_65_out, xnor_1_out);
  or or_9 (or_9_out, and_40_out, or_8_out, and_63_out);
  assign controlled_buffer_75_out = and_64_out ? and_66_out : 1'bz;  // Controlled_Buffer controlled_buffer_75
  and and_66 (and_66_out, controlled_buffer_76_out, not_5_out);
  not not_5 (not_5_out, or_8_out);
  assign controlled_buffer_76_out = not_6_out ? controlled_buffer_41_out : 1'bz;  // Controlled_Buffer controlled_buffer_76
  not not_6 (not_6_out, and_40_out);
  and and_67 (and_67_out, Instruction[11], and_42_out);
  and and_68 (and_68_out, ~Instruction[12], and_42_out);  // AND_Gate
  assign controlled_buffer_77_out = and_44_out ? Program_Address[4] : 1'bz;  // Controlled_Buffer controlled_buffer_77
  assign controlled_buffer_78_out = and_44_out ? Program_Address[3] : 1'bz;  // Controlled_Buffer controlled_buffer_78
  assign controlled_buffer_79_out = and_44_out ? Program_Address[5] : 1'bz;  // Controlled_Buffer controlled_buffer_79
  assign controlled_buffer_80_out = and_44_out ? Program_Address[2] : 1'bz;  // Controlled_Buffer controlled_buffer_80
  assign controlled_buffer_74_out = or_9_out ? and_69_out : 1'bz;  // Controlled_Buffer controlled_buffer_81
  assign controlled_buffer_73_out = or_9_out ? and_66_out : 1'bz;  // Controlled_Buffer controlled_buffer_82
  assign controlled_buffer_83_out = and_64_out ? and_69_out : 1'bz;  // Controlled_Buffer controlled_buffer_83
  assign controlled_buffer_84_out = and_64_out ? and_70_out : 1'bz;  // Controlled_Buffer controlled_buffer_84
  and and_69 (and_69_out, controlled_buffer_86_out, not_5_out);
  and and_70 (and_70_out, controlled_buffer_87_out, not_5_out);
  assign controlled_buffer_76_out = and_40_out ? controlled_buffer_42_out : 1'bz;  // Controlled_Buffer controlled_buffer_85
  assign controlled_buffer_86_out = and_40_out ? controlled_buffer_44_out : 1'bz;  // Controlled_Buffer controlled_buffer_86
  assign controlled_buffer_87_out = not_6_out ? controlled_buffer_45_out : 1'bz;  // Controlled_Buffer controlled_buffer_87
  assign controlled_buffer_86_out = not_6_out ? controlled_buffer_43_out : 1'bz;  // Controlled_Buffer controlled_buffer_88
  or or_10 (or_10_out, and_59_out, and_67_out);
  or or_11 (or_11_out, and_60_out, and_68_out);
  assign controlled_buffer_89_out = and_44_out ? Program_Address[1] : 1'bz;  // Controlled_Buffer controlled_buffer_89
  assign controlled_buffer_90_out = and_44_out ? Program_Address[0] : 1'bz;  // Controlled_Buffer controlled_buffer_90
  assign controlled_buffer_75_out = or_12_out ? Instruction[7] : 1'bz;  // Controlled_Buffer controlled_buffer_91
  and and_71 (and_71_out, ~and_34_out, and_44_out);  // AND_Gate
  assign controlled_buffer_77_out = or_9_out ? and_72_out : 1'bz;  // Controlled_Buffer controlled_buffer_92
  assign controlled_buffer_79_out = or_9_out ? and_70_out : 1'bz;  // Controlled_Buffer controlled_buffer_93
  assign controlled_buffer_94_out = and_64_out ? and_73_out : 1'bz;  // Controlled_Buffer controlled_buffer_94
  assign controlled_buffer_95_out = and_64_out ? and_72_out : 1'bz;  // Controlled_Buffer controlled_buffer_95
  and and_72 (and_72_out, controlled_buffer_97_out, not_5_out);
  and and_73 (and_73_out, controlled_buffer_99_out, not_5_out);
  assign controlled_buffer_87_out = and_40_out ? controlled_buffer_46_out : 1'bz;  // Controlled_Buffer controlled_buffer_96
  assign controlled_buffer_97_out = and_40_out ? controlled_buffer_48_out : 1'bz;  // Controlled_Buffer controlled_buffer_97
  assign controlled_buffer_97_out = not_6_out ? controlled_buffer_47_out : 1'bz;  // Controlled_Buffer controlled_buffer_98
  assign controlled_buffer_99_out = not_6_out ? controlled_buffer_49_out : 1'bz;  // Controlled_Buffer controlled_buffer_99
  assign controlled_buffer_84_out = or_12_out ? Instruction[5] : 1'bz;  // Controlled_Buffer controlled_buffer_100
  assign controlled_buffer_94_out = or_12_out ? Instruction[3] : 1'bz;  // Controlled_Buffer controlled_buffer_101
  assign controlled_buffer_83_out = or_12_out ? Instruction[6] : 1'bz;  // Controlled_Buffer controlled_buffer_102
  assign controlled_buffer_95_out = or_12_out ? Instruction[4] : 1'bz;  // Controlled_Buffer controlled_buffer_103
  or or_12 (or_12_out, xnor_1_out, and_40_out, and_63_out, and_71_out);
  assign controlled_buffer_80_out = or_9_out ? and_74_out : 1'bz;  // Controlled_Buffer controlled_buffer_104
  assign controlled_buffer_78_out = or_9_out ? and_73_out : 1'bz;  // Controlled_Buffer controlled_buffer_105
  assign controlled_buffer_106_out = and_64_out ? and_74_out : 1'bz;  // Controlled_Buffer controlled_buffer_106
  assign controlled_buffer_107_out = and_64_out ? and_75_out : 1'bz;  // Controlled_Buffer controlled_buffer_107
  and and_74 (and_74_out, controlled_buffer_109_out, not_5_out);
  and and_75 (and_75_out, controlled_buffer_111_out, not_5_out);
  assign controlled_buffer_99_out = and_40_out ? controlled_buffer_50_out : 1'bz;  // Controlled_Buffer controlled_buffer_108
  assign controlled_buffer_109_out = and_40_out ? controlled_buffer_52_out : 1'bz;  // Controlled_Buffer controlled_buffer_109
  assign controlled_buffer_109_out = not_6_out ? controlled_buffer_51_out : 1'bz;  // Controlled_Buffer controlled_buffer_110
  assign controlled_buffer_111_out = not_6_out ? controlled_buffer_53_out : 1'bz;  // Controlled_Buffer controlled_buffer_111
  D_Flip_Flop d_ff_25 (
    .clk(and_19_out), .D(controlled_buffer_23_out), .Q(d_ff_25_q), .reset(not_1_out));  // open: Qn, preset, en
  assign controlled_buffer_41_out = and_23_out ? d_ff_25_q : 1'bz;  // Controlled_Buffer controlled_buffer_112
  assign controlled_buffer_43_out = and_23_out ? d_ff_26_q : 1'bz;  // Controlled_Buffer controlled_buffer_113
  D_Flip_Flop d_ff_26 (
    .clk(and_19_out), .D(controlled_buffer_24_out), .Q(d_ff_26_q), .reset(not_1_out));  // open: Qn, preset, en
  assign controlled_buffer_45_out = and_23_out ? d_ff_27_q : 1'bz;  // Controlled_Buffer controlled_buffer_114
  D_Flip_Flop d_ff_27 (
    .clk(and_19_out), .D(controlled_buffer_25_out), .Q(d_ff_27_q), .reset(not_1_out));  // open: Qn, preset, en
  assign controlled_buffer_47_out = and_23_out ? d_ff_28_q : 1'bz;  // Controlled_Buffer controlled_buffer_115
  D_Flip_Flop d_ff_28 (
    .clk(and_19_out), .D(controlled_buffer_26_out), .Q(d_ff_28_q), .reset(not_1_out));  // open: Qn, preset, en
  assign controlled_buffer_49_out = and_23_out ? d_ff_29_q : 1'bz;  // Controlled_Buffer controlled_buffer_116
  D_Flip_Flop d_ff_29 (
    .clk(and_19_out), .D(controlled_buffer_27_out), .Q(d_ff_29_q), .reset(not_1_out));  // open: Qn, preset, en
  assign controlled_buffer_51_out = and_23_out ? d_ff_30_q : 1'bz;  // Controlled_Buffer controlled_buffer_117
  D_Flip_Flop d_ff_30 (
    .clk(and_19_out), .D(controlled_buffer_28_out), .Q(d_ff_30_q), .reset(not_1_out));  // open: Qn, preset, en
  D_Flip_Flop d_ff_31 (
    .clk(and_19_out), .D(controlled_buffer_29_out), .Q(d_ff_31_q), .reset(not_1_out));  // open: Qn, preset, en
  assign controlled_buffer_53_out = and_23_out ? d_ff_31_q : 1'bz;  // Controlled_Buffer controlled_buffer_118
  D_Flip_Flop d_ff_32 (
    .clk(and_19_out), .D(controlled_buffer_30_out), .Q(d_ff_32_q), .reset(not_1_out));  // open: Qn, preset, en
  assign controlled_buffer_55_out = and_23_out ? d_ff_32_q : 1'bz;  // Controlled_Buffer controlled_buffer_119
  D_Flip_Flop d_ff_33 (
    .clk(and_20_out), .D(controlled_buffer_23_out), .Q(d_ff_33_q), .reset(not_1_out));  // open: Qn, preset, en
  assign controlled_buffer_41_out = and_24_out ? d_ff_33_q : 1'bz;  // Controlled_Buffer controlled_buffer_120
  assign controlled_buffer_43_out = and_24_out ? d_ff_34_q : 1'bz;  // Controlled_Buffer controlled_buffer_121
  D_Flip_Flop d_ff_34 (
    .clk(and_20_out), .D(controlled_buffer_24_out), .Q(d_ff_34_q), .reset(not_1_out));  // open: Qn, preset, en
  assign controlled_buffer_45_out = and_24_out ? d_ff_35_q : 1'bz;  // Controlled_Buffer controlled_buffer_122
  D_Flip_Flop d_ff_35 (
    .clk(and_20_out), .D(controlled_buffer_25_out), .Q(d_ff_35_q), .reset(not_1_out));  // open: Qn, preset, en
  D_Flip_Flop d_ff_36 (
    .clk(and_20_out), .D(controlled_buffer_26_out), .Q(d_ff_36_q), .reset(not_1_out));  // open: Qn, preset, en
  assign controlled_buffer_47_out = and_24_out ? d_ff_36_q : 1'bz;  // Controlled_Buffer controlled_buffer_123
  D_Flip_Flop d_ff_37 (
    .clk(and_20_out), .D(controlled_buffer_27_out), .Q(d_ff_37_q), .reset(not_1_out));  // open: Qn, preset, en
  assign controlled_buffer_49_out = and_24_out ? d_ff_37_q : 1'bz;  // Controlled_Buffer controlled_buffer_124
  assign controlled_buffer_51_out = and_24_out ? d_ff_38_q : 1'bz;  // Controlled_Buffer controlled_buffer_125
  D_Flip_Flop d_ff_38 (
    .clk(and_20_out), .D(controlled_buffer_28_out), .Q(d_ff_38_q), .reset(not_1_out));  // open: Qn, preset, en
  assign controlled_buffer_53_out = and_24_out ? d_ff_39_q : 1'bz;  // Controlled_Buffer controlled_buffer_126
  D_Flip_Flop d_ff_39 (
    .clk(and_20_out), .D(controlled_buffer_29_out), .Q(d_ff_39_q), .reset(not_1_out));  // open: Qn, preset, en
  assign controlled_buffer_55_out = and_24_out ? d_ff_40_q : 1'bz;  // Controlled_Buffer controlled_buffer_127
  D_Flip_Flop d_ff_40 (
    .clk(and_20_out), .D(controlled_buffer_30_out), .Q(d_ff_40_q), .reset(not_1_out));  // open: Qn, preset, en
  assign controlled_buffer_128_out = or_12_out ? Instruction[0] : 1'bz;  // Controlled_Buffer controlled_buffer_128
  assign controlled_buffer_107_out = or_12_out ? Instruction[1] : 1'bz;  // Controlled_Buffer controlled_buffer_129
  assign controlled_buffer_106_out = or_12_out ? Instruction[2] : 1'bz;  // Controlled_Buffer controlled_buffer_130
  assign controlled_buffer_89_out = or_9_out ? and_75_out : 1'bz;  // Controlled_Buffer controlled_buffer_131
  assign controlled_buffer_90_out = or_9_out ? and_76_out : 1'bz;  // Controlled_Buffer controlled_buffer_132
  assign controlled_buffer_128_out = and_64_out ? and_76_out : 1'bz;  // Controlled_Buffer controlled_buffer_133
  and and_76 (and_76_out, controlled_buffer_135_out, not_5_out);
  assign controlled_buffer_111_out = and_40_out ? controlled_buffer_54_out : 1'bz;  // Controlled_Buffer controlled_buffer_134
  assign controlled_buffer_135_out = and_40_out ? controlled_buffer_56_out : 1'bz;  // Controlled_Buffer controlled_buffer_135
  assign controlled_buffer_135_out = not_6_out ? controlled_buffer_55_out : 1'bz;  // Controlled_Buffer controlled_buffer_136
  assign controlled_buffer_42_out = and_27_out ? d_ff_25_q : 1'bz;  // Controlled_Buffer controlled_buffer_137
  assign controlled_buffer_44_out = and_27_out ? d_ff_26_q : 1'bz;  // Controlled_Buffer controlled_buffer_138
  assign controlled_buffer_46_out = and_27_out ? d_ff_27_q : 1'bz;  // Controlled_Buffer controlled_buffer_139
  assign controlled_buffer_48_out = and_27_out ? d_ff_28_q : 1'bz;  // Controlled_Buffer controlled_buffer_140
  assign controlled_buffer_50_out = and_27_out ? d_ff_29_q : 1'bz;  // Controlled_Buffer controlled_buffer_141
  assign controlled_buffer_52_out = and_27_out ? d_ff_30_q : 1'bz;  // Controlled_Buffer controlled_buffer_142
  assign controlled_buffer_54_out = and_27_out ? d_ff_31_q : 1'bz;  // Controlled_Buffer controlled_buffer_143
  assign controlled_buffer_56_out = and_27_out ? d_ff_32_q : 1'bz;  // Controlled_Buffer controlled_buffer_144
  assign controlled_buffer_42_out = and_28_out ? d_ff_33_q : 1'bz;  // Controlled_Buffer controlled_buffer_145
  assign controlled_buffer_44_out = and_28_out ? d_ff_34_q : 1'bz;  // Controlled_Buffer controlled_buffer_146
  assign controlled_buffer_46_out = and_28_out ? d_ff_35_q : 1'bz;  // Controlled_Buffer controlled_buffer_147
  assign controlled_buffer_48_out = and_28_out ? d_ff_36_q : 1'bz;  // Controlled_Buffer controlled_buffer_148
  assign controlled_buffer_50_out = and_28_out ? d_ff_37_q : 1'bz;  // Controlled_Buffer controlled_buffer_149
  assign controlled_buffer_52_out = and_28_out ? d_ff_38_q : 1'bz;  // Controlled_Buffer controlled_buffer_150
  assign controlled_buffer_54_out = and_28_out ? d_ff_39_q : 1'bz;  // Controlled_Buffer controlled_buffer_151
  assign controlled_buffer_56_out = and_28_out ? d_ff_40_q : 1'bz;  // Controlled_Buffer controlled_buffer_152
  or or_13 (or_13_out, and_61_out, and_42_out);
  assign controlled_buffer_153_out = and_62_out ? Instruction[5] : 1'bz;  // Controlled_Buffer controlled_buffer_153
  assign controlled_buffer_154_out = and_62_out ? Instruction[4] : 1'bz;  // Controlled_Buffer controlled_buffer_154
  assign controlled_buffer_155_out = and_62_out ? Instruction[6] : 1'bz;  // Controlled_Buffer controlled_buffer_155
  assign controlled_buffer_156_out = and_62_out ? Instruction[7] : 1'bz;  // Controlled_Buffer controlled_buffer_156
  not not_7 (not_7_out, and_62_out);
  assign controlled_buffer_155_out = not_7_out ? controlled_buffer_44_out : 1'bz;  // Controlled_Buffer controlled_buffer_157
  assign controlled_buffer_156_out = not_7_out ? controlled_buffer_42_out : 1'bz;  // Controlled_Buffer controlled_buffer_158
  assign controlled_buffer_154_out = not_7_out ? controlled_buffer_48_out : 1'bz;  // Controlled_Buffer controlled_buffer_159
  assign controlled_buffer_153_out = not_7_out ? controlled_buffer_46_out : 1'bz;  // Controlled_Buffer controlled_buffer_160
  assign controlled_buffer_161_out = and_62_out ? Instruction[0] : 1'bz;  // Controlled_Buffer controlled_buffer_161
  assign controlled_buffer_162_out = and_62_out ? Instruction[1] : 1'bz;  // Controlled_Buffer controlled_buffer_162
  assign controlled_buffer_163_out = and_62_out ? Instruction[2] : 1'bz;  // Controlled_Buffer controlled_buffer_163
  assign controlled_buffer_164_out = and_62_out ? Instruction[3] : 1'bz;  // Controlled_Buffer controlled_buffer_164
  assign controlled_buffer_162_out = not_7_out ? controlled_buffer_54_out : 1'bz;  // Controlled_Buffer controlled_buffer_165
  assign controlled_buffer_161_out = not_7_out ? controlled_buffer_56_out : 1'bz;  // Controlled_Buffer controlled_buffer_166
  assign controlled_buffer_164_out = not_7_out ? controlled_buffer_50_out : 1'bz;  // Controlled_Buffer controlled_buffer_167
  assign controlled_buffer_163_out = not_7_out ? controlled_buffer_52_out : 1'bz;  // Controlled_Buffer controlled_buffer_168
  and and_77 (and_77_out, and_58_out, Instruction[0]);
  or or_14 (or_14_out, and_77_out, or_10_out);
  and and_78 (and_78_out, and_58_out, Instruction[1]);
  or or_15 (or_15_out, and_78_out, or_11_out);
  and and_79 (and_79_out, and_58_out, Instruction[2]);
  and and_80 (and_80_out, and_58_out, Instruction[3]);
  or or_16 (or_16_out, and_80_out, or_13_out);
  and and_81 (and_81_out, and_58_out, Instruction[4]);
  or or_17 (or_17_out, and_81_out, or_13_out);
  and and_82 (and_82_out, and_58_out, Instruction[5]);
  and and_83 (and_83_out, and_58_out, Instruction[6]);
  and and_84 (and_84_out, and_58_out, Instruction[7]);
  and and_85 (and_85_out, not_8_out, controlled_buffer_156_out);
  and and_86 (and_86_out, not_8_out, controlled_buffer_155_out);
  and and_87 (and_87_out, not_8_out, controlled_buffer_153_out);
  and and_88 (and_88_out, not_8_out, controlled_buffer_154_out);
  and and_89 (and_89_out, controlled_buffer_164_out, not_8_out);
  and and_90 (and_90_out, controlled_buffer_163_out, not_8_out);
  and and_91 (and_91_out, controlled_buffer_162_out, not_8_out);
  and and_92 (and_92_out, controlled_buffer_161_out, not_8_out);
  not not_8 (not_8_out, and_42_out);
  not not_9 (not_9_out, and_101_out);
  and and_93 (and_93_out, controlled_buffer_41_out, not_9_out);
  and and_94 (and_94_out, controlled_buffer_43_out, not_9_out);
  and and_95 (and_95_out, controlled_buffer_45_out, not_9_out);
  and and_96 (and_96_out, controlled_buffer_47_out, not_9_out);
  and and_97 (and_97_out, controlled_buffer_49_out, not_9_out);
  and and_98 (and_98_out, controlled_buffer_51_out, not_9_out);
  and and_99 (and_99_out, controlled_buffer_53_out, not_9_out);
  and and_100 (and_100_out, controlled_buffer_55_out, not_9_out);
  and and_101 (and_101_out, ~or_17_out, ~or_16_out, ~and_79_out, ~or_15_out, or_14_out);  // AND_Gate
  xor xor_25 (xor_25_out, and_85_out, or_22_out);
  and and_102 (and_102_out, or_19_out, xor_28_out);
  or or_18 (or_18_out, and_102_out, and_103_out);
  and and_103 (and_103_out, and_94_out, xor_29_out);
  xor xor_26 (xor_26_out, xor_25_out, or_18_out);
  xor xor_27 (xor_27_out, and_93_out, xor_26_out);
  and and_104 (and_104_out, xor_27_out, or_23_out);
  assign controlled_buffer_23_out = and_144_out ? and_104_out : 1'bz;  // Controlled_Buffer controlled_buffer_169
  xor xor_28 (xor_28_out, and_86_out, or_22_out);
  or or_19 (or_19_out, and_107_out, and_108_out);
  xor xor_29 (xor_29_out, xor_28_out, or_19_out);
  xor xor_30 (xor_30_out, and_94_out, xor_29_out);
  and and_105 (and_105_out, xor_30_out, or_23_out);
  assign controlled_buffer_24_out = and_144_out ? and_105_out : 1'bz;  // Controlled_Buffer controlled_buffer_170
  and and_106 (and_106_out, or_17_out, ~or_16_out, and_111_out);  // AND_Gate
  or or_20 (or_20_out, and_106_out, and_116_out);
  xor xor_31 (xor_31_out, and_87_out, or_22_out);
  and and_107 (and_107_out, or_24_out, xor_31_out);
  and and_108 (and_108_out, and_95_out, xor_32_out);
  xor xor_32 (xor_32_out, xor_31_out, or_24_out);
  xor xor_33 (xor_33_out, and_95_out, xor_32_out);
  and and_109 (and_109_out, xor_33_out, or_23_out);
  assign controlled_buffer_25_out = and_144_out ? and_109_out : 1'bz;  // Controlled_Buffer controlled_buffer_171
  and and_110 (and_110_out, ~or_17_out, ~or_16_out, ~and_79_out, or_15_out);  // AND_Gate
  and and_111 (and_111_out, and_79_out, or_15_out);
  and and_112 (and_112_out, or_14_out, and_115_out);
  or or_21 (or_21_out, or_20_out, and_112_out);
  or or_22 (or_22_out, or_20_out, and_115_out);
  or or_23 (or_23_out, and_101_out, and_110_out);
  and and_113 (and_113_out, or_26_out, xor_34_out);
  or or_24 (or_24_out, and_113_out, and_114_out);
  and and_114 (and_114_out, and_96_out, xor_35_out);
  and and_115 (and_115_out, or_17_out, or_16_out, ~and_79_out);  // AND_Gate
  and and_116 (and_116_out, and_110_out, or_14_out);
  xnor xnor_2 (xnor_2_out, or_15_out, or_14_out);
  and and_117 (and_117_out, and_115_out, xnor_2_out);
  or or_25 (or_25_out, or_23_out, and_106_out, and_115_out);
  xor xor_34 (xor_34_out, and_88_out, or_22_out);
  and and_118 (and_118_out, or_27_out, xor_37_out);
  or or_26 (or_26_out, and_118_out, and_119_out);
  and and_119 (and_119_out, and_97_out, xor_38_out);
  xor xor_35 (xor_35_out, xor_34_out, or_26_out);
  xor xor_36 (xor_36_out, and_96_out, xor_35_out);
  and and_120 (and_120_out, xor_36_out, or_23_out);
  assign controlled_buffer_26_out = and_144_out ? and_120_out : 1'bz;  // Controlled_Buffer controlled_buffer_172
  and and_121 (and_121_out, or_17_out, ~or_16_out);  // AND_Gate
  and and_122 (and_122_out, ~and_111_out, and_121_out);  // AND_Gate
  xor xor_37 (xor_37_out, and_89_out, or_22_out);
  and and_123 (and_123_out, or_29_out, xor_40_out);
  or or_27 (or_27_out, and_123_out, and_124_out);
  and and_124 (and_124_out, and_98_out, xor_41_out);
  xor xor_38 (xor_38_out, xor_37_out, or_27_out);
  xor xor_39 (xor_39_out, and_97_out, xor_38_out);
  and and_125 (and_125_out, xor_39_out, or_23_out);
  assign controlled_buffer_27_out = and_144_out ? and_125_out : 1'bz;  // Controlled_Buffer controlled_buffer_173
  and and_126 (and_126_out, and_79_out, ~or_15_out);  // AND_Gate
  and and_127 (and_127_out, ~and_79_out, or_15_out);  // AND_Gate
  and and_128 (and_128_out, and_126_out, and_84_out);
  or or_28 (or_28_out, and_128_out, and_127_out);
  and and_129 (and_129_out, and_121_out, or_31_out);
  and and_130 (and_130_out, and_121_out, or_28_out);
  xor xor_40 (xor_40_out, and_90_out, or_22_out);
  or or_29 (or_29_out, and_135_out, and_136_out);
  xor xor_41 (xor_41_out, xor_40_out, or_29_out);
  xor xor_42 (xor_42_out, and_98_out, xor_41_out);
  and and_131 (and_131_out, xor_42_out, or_23_out);
  assign controlled_buffer_28_out = and_144_out ? and_131_out : 1'bz;  // Controlled_Buffer controlled_buffer_174
  and and_132 (and_132_out, ~and_79_out, ~or_14_out);  // AND_Gate
  and and_133 (and_133_out, ~and_79_out, or_14_out);  // AND_Gate
  or or_30 (or_30_out, and_126_out, and_133_out);
  or or_31 (or_31_out, and_126_out, and_132_out);
  and and_134 (and_134_out, and_121_out, or_30_out);
  xor xor_43 (xor_43_out, and_91_out, or_22_out);
  and and_135 (and_135_out, or_33_out, xor_43_out);
  and and_136 (and_136_out, and_99_out, xor_44_out);
  xor xor_44 (xor_44_out, xor_43_out, or_33_out);
  xor xor_45 (xor_45_out, and_99_out, xor_44_out);
  or or_32 (or_32_out, xor_27_out, xor_45_out, xor_49_out, xor_42_out, xor_39_out, xor_36_out, xor_33_out, xor_30_out);
  and and_137 (and_137_out, or_23_out, xor_45_out);
  assign controlled_buffer_29_out = and_144_out ? and_137_out : 1'bz;  // Controlled_Buffer controlled_buffer_175
  and and_138 (and_138_out, or_21_out, xor_47_out);
  or or_33 (or_33_out, and_138_out, and_139_out);
  and and_139 (and_139_out, and_100_out, xor_48_out);
  and and_140 (and_140_out, xor_27_out, and_115_out);
  and and_141 (and_141_out, or_32_out, ~and_115_out);  // AND_Gate
  or or_34 (or_34_out, and_141_out, and_140_out);
  xor xor_46 (xor_46_out, or_34_out, and_117_out);
  and and_142 (and_142_out, or_23_out, xor_49_out);
  and and_143 (and_143_out, ~or_23_out, xor_46_out);  // AND_Gate
  and and_144 (and_144_out, ~and_42_out, or_25_out);  // AND_Gate
  or or_35 (or_35_out, and_143_out, and_142_out);
  assign controlled_buffer_30_out = and_144_out ? or_35_out : 1'bz;  // Controlled_Buffer controlled_buffer_176
  xor xor_47 (xor_47_out, and_92_out, or_22_out);
  xor xor_48 (xor_48_out, xor_47_out, or_21_out);
  xor xor_49 (xor_49_out, and_100_out, xor_48_out);
  or or_36 (or_36_out, and_94_out, and_95_out, and_96_out, and_97_out, and_98_out, and_99_out, and_100_out);
  and and_145 (and_145_out, ~and_93_out, or_36_out);  // AND_Gate
  and and_146 (and_146_out, and_145_out, and_147_out, ~and_134_out, and_129_out);  // AND_Gate
  assign controlled_buffer_177_out = and_122_out ? 1'b0 : 1'bz;  // Controlled_Buffer controlled_buffer_177
  buf buffer_1 (controlled_buffer_23_out, controlled_buffer_177_out);
  buf buffer_2 (controlled_buffer_24_out, controlled_buffer_177_out);
  buf buffer_3 (controlled_buffer_25_out, controlled_buffer_177_out);
  buf buffer_4 (controlled_buffer_26_out, controlled_buffer_177_out);
  buf buffer_5 (controlled_buffer_27_out, controlled_buffer_177_out);
  buf buffer_6 (controlled_buffer_28_out, controlled_buffer_177_out);
  buf buffer_7 (controlled_buffer_29_out, controlled_buffer_177_out);
  and and_147 (and_147_out, ~and_85_out, or_39_out);  // AND_Gate
  or or_37 (or_37_out, and_147_out, and_145_out);
  xor xor_50 (xor_50_out, and_147_out, and_145_out);
  and and_148 (and_148_out, ~and_129_out, and_134_out, or_37_out);  // AND_Gate
  and and_149 (and_149_out, and_134_out, and_129_out, xor_50_out);
  or or_38 (or_38_out, and_146_out, and_148_out, and_149_out);
  xor xor_51 (xor_51_out, and_130_out, or_38_out);
  assign controlled_buffer_30_out = and_122_out ? xor_51_out : 1'bz;  // Controlled_Buffer controlled_buffer_178
  or or_39 (or_39_out, and_86_out, and_87_out, and_88_out, and_89_out, and_90_out, and_91_out, and_92_out);

  // Notes on the sheet:
  //   source
  //   target
  //   write
endmodule

module Comp (
  input  in_1,
  input  in_2
);

  wire and_1_out, cpu_1_clock, cpu_1_com, Ex_out, not_1_out, not_2_out, undriven_2;
  wire [7:0] cpu_1_program_address, ram_1_data, undriven;
  wire [15:0] rom_1_data;

  and and_1 (and_1_out, ~cpu_1_clock, undriven_2);  // AND_Gate
  not not_1 (not_1_out, cpu_1_com);
  not not_2 (not_2_out, in_1);
  RAM #(.bus("asynch")) ram_1 (.addr(undriven), .data(ram_1_data), .sel(and_1_out), .ld(not_1_out), .clr(not_2_out));
  Button Ex (.out(Ex_out));
  CPU cpu_1 (
    .Power(in_1), .Sleep(in_2), .Trigger(Ex_out), .COM(cpu_1_com), .I_O(ram_1_data),
    .Program_Address(cpu_1_program_address), .Instruction(rom_1_data), .Clock(cpu_1_clock));  // open: Write, Address
  ROM #(.dataWidth(16)) rom_1 (.addr(cpu_1_program_address), .data(rom_1_data));  // open: sel

  // Notes on the sheet:
  //   contents of rom_1 (hex, n*v repeats v):
  //   4*0 1301 ce01 8800 c419 5006 8800 98ff 9900 1e01 42f8 1b01 ce01 261f 42f3 42f3 f000
endmodule

module Test (
  input  Power,
  input  Sleep,
  input  Trigger
);

  wire and_9_out, and_10_out, and_11_out, and_12_out, and_13_out, and_14_out, and_15_out, and_16_out,
       and_17_out, and_18_out, and_19_out, and_20_out, and_21_out, and_22_out, and_23_out, and_24_out,
       and_25_out, and_26_out, and_27_out, and_28_out, and_29_out, and_30_out, and_31_out, and_32_out,
       and_33_out, and_34_out, and_35_out, and_36_out, and_37_out, and_38_out, and_39_out, and_40_out,
       and_41_out, and_42_out, and_43_out, and_44_out, and_45_out, and_46_out, and_47_out, and_48_out,
       and_49_out, and_50_out, and_51_out, and_52_out, and_53_out, and_54_out, and_55_out, and_56_out,
       and_57_out, and_58_out, and_59_out, and_60_out, and_61_out, and_62_out, and_63_out, and_64_out,
       and_65_out, and_66_out, and_67_out, and_68_out, and_69_out, and_70_out, and_71_out, and_72_out,
       and_73_out, and_74_out, and_75_out, and_76_out, and_77_out, and_78_out, and_79_out, and_80_out,
       and_81_out, and_82_out, and_83_out, and_84_out, and_85_out, and_86_out, and_87_out, and_88_out,
       and_89_out, and_90_out, and_91_out, and_92_out, and_93_out, and_94_out, and_95_out, and_96_out,
       and_97_out, and_98_out, and_99_out, and_100_out, and_101_out, and_102_out, and_103_out, and_104_out,
       and_105_out, and_106_out, and_107_out, and_108_out, and_109_out, and_110_out, and_111_out,
       and_112_out, and_113_out, and_114_out, and_115_out, and_116_out, and_117_out, and_118_out,
       and_119_out, and_120_out, and_121_out, and_122_out, and_123_out, and_124_out, and_125_out,
       and_126_out, and_127_out, and_128_out, and_129_out, and_130_out, and_131_out, and_132_out,
       and_133_out, and_134_out, and_135_out, and_136_out, and_137_out, and_138_out, and_139_out,
       and_140_out, and_141_out, and_142_out, and_143_out, and_144_out, and_145_out, and_146_out,
       and_147_out, and_148_out, and_149_out, clock_1_out, controlled_buffer_1_out, controlled_buffer_2_out,
       controlled_buffer_5_out, controlled_buffer_6_out, controlled_buffer_7_out, controlled_buffer_8_out,
       controlled_buffer_21_out, controlled_buffer_22_out, controlled_buffer_23_out,
       controlled_buffer_24_out, controlled_buffer_25_out, controlled_buffer_26_out,
       controlled_buffer_27_out, controlled_buffer_28_out, controlled_buffer_29_out,
       controlled_buffer_30_out, controlled_buffer_41_out, controlled_buffer_42_out,
       controlled_buffer_43_out, controlled_buffer_44_out, controlled_buffer_45_out,
       controlled_buffer_46_out, controlled_buffer_47_out, controlled_buffer_48_out,
       controlled_buffer_49_out, controlled_buffer_50_out, controlled_buffer_51_out,
       controlled_buffer_52_out, controlled_buffer_53_out, controlled_buffer_54_out,
       controlled_buffer_55_out, controlled_buffer_56_out, controlled_buffer_73_out,
       controlled_buffer_74_out, controlled_buffer_75_out, controlled_buffer_76_out,
       controlled_buffer_77_out, controlled_buffer_78_out, controlled_buffer_79_out,
       controlled_buffer_82_out, controlled_buffer_83_out, controlled_buffer_85_out,
       controlled_buffer_87_out, controlled_buffer_88_out, controlled_buffer_89_out,
       controlled_buffer_90_out, controlled_buffer_94_out, controlled_buffer_95_out,
       controlled_buffer_96_out, controlled_buffer_98_out, controlled_buffer_106_out,
       controlled_buffer_107_out, controlled_buffer_109_out, controlled_buffer_110_out,
       controlled_buffer_122_out, controlled_buffer_127_out, controlled_buffer_153_out,
       controlled_buffer_154_out, controlled_buffer_155_out, controlled_buffer_159_out,
       controlled_buffer_160_out, controlled_buffer_161_out, controlled_buffer_162_out,
       controlled_buffer_167_out, controlled_buffer_177_out, d_ff_9_q, d_ff_10_q, d_ff_11_q, d_ff_12_q,
       d_ff_13_q, d_ff_14_q, d_ff_15_q, d_ff_16_q, d_ff_17_q, d_ff_18_q, d_ff_19_q, d_ff_20_q, d_ff_21_q,
       d_ff_22_q, d_ff_23_q, d_ff_24_q, d_ff_25_q, d_ff_26_q, d_ff_27_q, d_ff_28_q, d_ff_29_q, d_ff_30_q,
       d_ff_31_q, d_ff_32_q, d_ff_33_q, d_ff_34_q, d_ff_35_q, d_ff_36_q, d_ff_37_q, d_ff_38_q, d_ff_39_q,
       d_ff_40_q, ex_out, not_1_out, not_2_out, not_3_out, not_4_out, not_5_out, not_6_out, not_7_out,
       not_8_out, not_9_out, not_10_out, not_11_out, or_1_out, or_2_out, or_3_out, or_4_out, or_5_out,
       or_6_out, or_7_out, or_8_out, or_9_out, or_10_out, or_11_out, or_12_out, or_13_out, or_14_out,
       or_15_out, or_16_out, or_17_out, or_18_out, or_19_out, or_20_out, or_21_out, or_22_out, or_23_out,
       or_24_out, or_25_out, or_26_out, or_27_out, or_28_out, or_29_out, or_30_out, or_31_out, or_32_out,
       or_33_out, or_34_out, or_35_out, or_36_out, or_37_out, or_38_out, or_39_out, xnor_1_out, xnor_2_out,
       xor_1_out, xor_2_out, xor_3_out, xor_4_out, xor_5_out, xor_6_out, xor_7_out, xor_8_out, xor_9_out,
       xor_10_out, xor_11_out, xor_12_out, xor_13_out, xor_14_out, xor_15_out, xor_16_out, xor_17_out,
       xor_18_out, xor_19_out, xor_20_out, xor_21_out, xor_22_out, xor_23_out, xor_24_out, xor_25_out,
       xor_26_out, xor_27_out, xor_28_out, xor_29_out, xor_30_out, xor_31_out, xor_32_out, xor_33_out,
       xor_34_out, xor_35_out, xor_36_out, xor_37_out, xor_38_out, xor_39_out, xor_40_out, xor_41_out,
       xor_42_out, xor_43_out, xor_44_out, xor_45_out, xor_46_out, xor_47_out, xor_48_out, xor_49_out,
       xor_50_out, xor_51_out;
  wire [7:0] and_8_out, d_ff_8_q, ram_1_data;
  wire [15:0] rom_1_data;

  RAM ram_1 (.addr(and_8_out), .data(ram_1_data), .clk(not_1_out), .ld(not_2_out), .clr(not_3_out));  // open: sel
  Button ex (.out(ex_out));
  not not_1 (not_1_out, and_10_out);
  not not_2 (not_2_out, and_35_out);
  not not_3 (not_3_out, Power);
  assign controlled_buffer_1_out = not_4_out ? not_6_out : 1'bz;  // Controlled_Buffer controlled_buffer_1
  assign controlled_buffer_2_out = not_4_out ? xor_2_out : 1'bz;  // Controlled_Buffer controlled_buffer_2
  not not_4 (not_4_out, and_31_out);
  assign controlled_buffer_2_out = and_31_out ? xor_15_out : 1'bz;  // Controlled_Buffer controlled_buffer_3
  assign controlled_buffer_1_out = and_31_out ? xor_24_out : 1'bz;  // Controlled_Buffer controlled_buffer_4
  and and_1 (and_8_out[7], and_39_out, xor_9_out);
  and and_2 (and_8_out[6], and_39_out, xor_10_out);
  and and_3 (and_8_out[5], and_39_out, xor_11_out);
  and and_4 (and_8_out[4], and_39_out, xor_12_out);
  and and_5 (and_8_out[3], and_39_out, xor_13_out);
  and and_6 (and_8_out[2], and_39_out, xor_14_out);
  and and_7 (and_8_out[1], and_39_out, xor_15_out);
  and and_8 (and_8_out[0], and_39_out, xor_24_out);
  Clock clock_1 (.out(clock_1_out));
  and and_9 (and_9_out, ~Sleep, clock_1_out);  // AND_Gate
  ExactlyOne xor_1 (.out(xor_1_out), .in0(and_9_out), .in1(ex_out), .in2(Trigger));
  and and_10 (and_10_out, ~and_32_out, Power, xor_1_out);  // AND_Gate
  assign controlled_buffer_5_out = not_4_out ? xor_6_out : 1'bz;  // Controlled_Buffer controlled_buffer_5
  assign controlled_buffer_6_out = not_4_out ? xor_5_out : 1'bz;  // Controlled_Buffer controlled_buffer_6
  assign controlled_buffer_7_out = not_4_out ? xor_3_out : 1'bz;  // Controlled_Buffer controlled_buffer_7
  assign controlled_buffer_8_out = not_4_out ? xor_4_out : 1'bz;  // Controlled_Buffer controlled_buffer_8
  assign controlled_buffer_8_out = and_31_out ? xor_13_out : 1'bz;  // Controlled_Buffer controlled_buffer_9
  assign controlled_buffer_5_out = and_31_out ? xor_11_out : 1'bz;  // Controlled_Buffer controlled_buffer_10
  assign controlled_buffer_6_out = and_31_out ? xor_12_out : 1'bz;  // Controlled_Buffer controlled_buffer_11
  assign controlled_buffer_7_out = and_31_out ? xor_14_out : 1'bz;  // Controlled_Buffer controlled_buffer_12
  and and_11 (and_11_out, and_39_out, ~and_35_out);  // AND_Gate
  and and_12 (and_12_out, and_39_out, and_35_out);
  not not_5 (not_5_out, and_10_out);
  assign ram_1_data[7] = and_12_out ? controlled_buffer_41_out : 1'bz;  // Controlled_Buffer controlled_buffer_13
  assign ram_1_data[6] = and_12_out ? controlled_buffer_43_out : 1'bz;  // Controlled_Buffer controlled_buffer_14
  assign ram_1_data[5] = and_12_out ? controlled_buffer_45_out : 1'bz;  // Controlled_Buffer controlled_buffer_15
  assign ram_1_data[4] = and_12_out ? controlled_buffer_47_out : 1'bz;  // Controlled_Buffer controlled_buffer_16
  assign ram_1_data[3] = and_12_out ? controlled_buffer_49_out : 1'bz;  // Controlled_Buffer controlled_buffer_17
  assign ram_1_data[2] = and_12_out ? controlled_buffer_51_out : 1'bz;  // Controlled_Buffer controlled_buffer_18
  assign ram_1_data[1] = and_12_out ? controlled_buffer_53_out : 1'bz;  // Controlled_Buffer controlled_buffer_19
  assign ram_1_data[0] = and_12_out ? controlled_buffer_55_out : 1'bz;  // Controlled_Buffer controlled_buffer_20
  assign controlled_buffer_21_out = and_11_out ? ram_1_data[7] : 1'bz;  // Controlled_Buffer controlled_buffer_21
  assign controlled_buffer_22_out = and_11_out ? ram_1_data[6] : 1'bz;  // Controlled_Buffer controlled_buffer_22
  assign controlled_buffer_23_out = and_11_out ? ram_1_data[5] : 1'bz;  // Controlled_Buffer controlled_buffer_23
  assign controlled_buffer_24_out = and_11_out ? ram_1_data[4] : 1'bz;  // Controlled_Buffer controlled_buffer_24
  assign controlled_buffer_25_out = and_11_out ? ram_1_data[3] : 1'bz;  // Controlled_Buffer controlled_buffer_25
  assign controlled_buffer_26_out = and_11_out ? ram_1_data[2] : 1'bz;  // Controlled_Buffer controlled_buffer_26
  assign controlled_buffer_27_out = and_11_out ? ram_1_data[1] : 1'bz;  // Controlled_Buffer controlled_buffer_27
  assign controlled_buffer_28_out = and_11_out ? ram_1_data[0] : 1'bz;  // Controlled_Buffer controlled_buffer_28
  not not_6 (not_6_out, d_ff_8_q[0]);
  xor xor_2 (xor_2_out, d_ff_8_q[0], d_ff_8_q[1]);
  and and_13 (and_13_out, d_ff_8_q[1], d_ff_8_q[0]);
  xor xor_3 (xor_3_out, and_13_out, d_ff_8_q[2]);
  and and_14 (and_14_out, d_ff_8_q[2], and_13_out);
  xor xor_4 (xor_4_out, and_14_out, d_ff_8_q[3]);
  and and_15 (and_15_out, d_ff_8_q[3], and_14_out);
  xor xor_5 (xor_5_out, and_15_out, d_ff_8_q[4]);
  and and_16 (and_16_out, d_ff_8_q[4], and_15_out);
  xor xor_6 (xor_6_out, and_16_out, d_ff_8_q[5]);
  and and_17 (and_17_out, d_ff_8_q[5], and_16_out);
  xor xor_7 (xor_7_out, and_17_out, d_ff_8_q[6]);
  and and_18 (and_18_out, d_ff_8_q[6], and_17_out);
  xor xor_8 (xor_8_out, and_18_out, d_ff_8_q[7]);
  assign controlled_buffer_29_out = not_4_out ? xor_8_out : 1'bz;  // Controlled_Buffer controlled_buffer_29
  assign controlled_buffer_30_out = not_4_out ? xor_7_out : 1'bz;  // Controlled_Buffer controlled_buffer_30
  assign controlled_buffer_30_out = and_31_out ? xor_10_out : 1'bz;  // Controlled_Buffer controlled_buffer_31
  assign controlled_buffer_29_out = and_31_out ? xor_9_out : 1'bz;  // Controlled_Buffer controlled_buffer_32
  and and_19 (and_19_out, rom_1_data[8], not_5_out, rom_1_data[9]);
  and and_20 (and_20_out, ~rom_1_data[8], not_5_out, rom_1_data[9]);  // AND_Gate
  and and_21 (and_21_out, rom_1_data[8], not_5_out, ~rom_1_data[9]);  // AND_Gate
  and and_22 (and_22_out, ~rom_1_data[8], not_5_out, ~rom_1_data[9]);  // AND_Gate
  and and_23 (and_23_out, rom_1_data[8], rom_1_data[9]);
  and and_24 (and_24_out, ~rom_1_data[8], rom_1_data[9]);  // AND_Gate
  and and_25 (and_25_out, rom_1_data[8], ~rom_1_data[9]);  // AND_Gate
  and and_26 (and_26_out, ~rom_1_data[8], ~rom_1_data[9]);  // AND_Gate
  and and_27 (and_27_out, rom_1_data[10], rom_1_data[11]);
  and and_28 (and_28_out, ~rom_1_data[10], rom_1_data[11]);  // AND_Gate
  and and_29 (and_29_out, rom_1_data[10], ~rom_1_data[11]);  // AND_Gate
  and and_30 (and_30_out, ~rom_1_data[10], ~rom_1_data[11]);  // AND_Gate
  D_Flip_Flop d_ff_1 (
    .clk(and_10_out), .D(controlled_buffer_29_out), .Q(d_ff_8_q[7]), .reset(not_3_out));  // open: Qn, preset, en
  D_Flip_Flop d_ff_2 (
    .clk(and_10_out), .D(controlled_buffer_30_out), .Q(d_ff_8_q[6]), .reset(not_3_out));  // open: Qn, preset, en
  D_Flip_Flop d_ff_3 (
    .clk(and_10_out), .D(controlled_buffer_5_out), .Q(d_ff_8_q[5]), .reset(not_3_out));  // open: Qn, preset, en
  D_Flip_Flop d_ff_4 (
    .clk(and_10_out), .D(controlled_buffer_6_out), .Q(d_ff_8_q[4]), .reset(not_3_out));  // open: Qn, preset, en
  D_Flip_Flop d_ff_5 (
    .clk(and_10_out), .D(controlled_buffer_8_out), .Q(d_ff_8_q[3]), .reset(not_3_out));  // open: Qn, preset, en
  D_Flip_Flop d_ff_6 (
    .clk(and_10_out), .D(controlled_buffer_7_out), .Q(d_ff_8_q[2]), .reset(not_3_out));  // open: Qn, preset, en
  D_Flip_Flop d_ff_7 (
    .clk(and_10_out), .D(controlled_buffer_2_out), .Q(d_ff_8_q[1]), .reset(not_3_out));  // open: Qn, preset, en
  D_Flip_Flop d_ff_8 (
    .clk(and_10_out), .D(controlled_buffer_1_out), .Q(d_ff_8_q[0]), .reset(not_3_out));  // open: Qn, preset, en
  assign controlled_buffer_26_out = and_33_out ? d_ff_8_q[5] : 1'bz;  // Controlled_Buffer controlled_buffer_33
  assign controlled_buffer_27_out = and_33_out ? d_ff_8_q[6] : 1'bz;  // Controlled_Buffer controlled_buffer_34
  assign controlled_buffer_28_out = and_33_out ? d_ff_8_q[7] : 1'bz;  // Controlled_Buffer controlled_buffer_35
  assign controlled_buffer_25_out = and_33_out ? d_ff_8_q[4] : 1'bz;  // Controlled_Buffer controlled_buffer_36
  and and_31 (and_31_out, ~xor_46_out, and_62_out);  // AND_Gate
  assign controlled_buffer_22_out = and_33_out ? d_ff_8_q[1] : 1'bz;  // Controlled_Buffer controlled_buffer_37
  assign controlled_buffer_24_out = and_33_out ? d_ff_8_q[3] : 1'bz;  // Controlled_Buffer controlled_buffer_38
  assign controlled_buffer_23_out = and_33_out ? d_ff_8_q[2] : 1'bz;  // Controlled_Buffer controlled_buffer_39
  assign controlled_buffer_21_out = and_33_out ? d_ff_8_q[0] : 1'bz;  // Controlled_Buffer controlled_buffer_40
  D_Flip_Flop d_ff_9 (
    .clk(and_21_out), .D(controlled_buffer_21_out), .Q(d_ff_9_q), .reset(not_3_out));  // open: Qn, preset, en
  D_Flip_Flop d_ff_10 (
    .clk(and_21_out), .D(controlled_buffer_22_out), .Q(d_ff_10_q), .reset(not_3_out));  // open: Qn, preset, en
  D_Flip_Flop d_ff_11 (
    .clk(and_21_out), .D(controlled_buffer_23_out), .Q(d_ff_11_q), .reset(not_3_out));  // open: Qn, preset, en
  D_Flip_Flop d_ff_12 (
    .clk(and_21_out), .D(controlled_buffer_24_out), .Q(d_ff_12_q), .reset(not_3_out));  // open: Qn, preset, en
  D_Flip_Flop d_ff_13 (
    .clk(and_21_out), .D(controlled_buffer_25_out), .Q(d_ff_13_q), .reset(not_3_out));  // open: Qn, preset, en
  D_Flip_Flop d_ff_14 (
    .clk(and_21_out), .D(controlled_buffer_26_out), .Q(d_ff_14_q), .reset(not_3_out));  // open: Qn, preset, en
  D_Flip_Flop d_ff_15 (
    .clk(and_21_out), .D(controlled_buffer_27_out), .Q(d_ff_15_q), .reset(not_3_out));  // open: Qn, preset, en
  D_Flip_Flop d_ff_16 (
    .clk(and_21_out), .D(controlled_buffer_28_out), .Q(d_ff_16_q), .reset(not_3_out));  // open: Qn, preset, en
  D_Flip_Flop d_ff_17 (
    .clk(and_22_out), .D(controlled_buffer_21_out), .Q(d_ff_17_q), .reset(not_3_out));  // open: Qn, preset, en
  D_Flip_Flop d_ff_18 (
    .clk(and_22_out), .D(controlled_buffer_22_out), .Q(d_ff_18_q), .reset(not_3_out));  // open: Qn, preset, en
  D_Flip_Flop d_ff_19 (
    .clk(and_22_out), .D(controlled_buffer_23_out), .Q(d_ff_19_q), .reset(not_3_out));  // open: Qn, preset, en
  D_Flip_Flop d_ff_20 (
    .clk(and_22_out), .D(controlled_buffer_24_out), .Q(d_ff_20_q), .reset(not_3_out));  // open: Qn, preset, en
  D_Flip_Flop d_ff_21 (
    .clk(and_22_out), .D(controlled_buffer_25_out), .Q(d_ff_21_q), .reset(not_3_out));  // open: Qn, preset, en
  D_Flip_Flop d_ff_22 (
    .clk(and_22_out), .D(controlled_buffer_26_out), .Q(d_ff_22_q), .reset(not_3_out));  // open: Qn, preset, en
  D_Flip_Flop d_ff_23 (
    .clk(and_22_out), .D(controlled_buffer_27_out), .Q(d_ff_23_q), .reset(not_3_out));  // open: Qn, preset, en
  D_Flip_Flop d_ff_24 (
    .clk(and_22_out), .D(controlled_buffer_28_out), .Q(d_ff_24_q), .reset(not_3_out));  // open: Qn, preset, en
  and and_32 (and_32_out, rom_1_data[15], rom_1_data[14], rom_1_data[13], rom_1_data[12]);
  and and_33 (and_33_out, rom_1_data[10], and_62_out);
  and and_34 (and_34_out, and_39_out, rom_1_data[13]);
  and and_35 (and_35_out, and_39_out, rom_1_data[12]);
  xor xor_9 (xor_9_out, controlled_buffer_73_out, xor_17_out);
  xor xor_10 (xor_10_out, controlled_buffer_76_out, xor_18_out);
  xor xor_11 (xor_11_out, controlled_buffer_78_out, xor_19_out);
  xor xor_12 (xor_12_out, controlled_buffer_77_out, xor_20_out);
  xor xor_13 (xor_13_out, controlled_buffer_79_out, xor_21_out);
  xor xor_14 (xor_14_out, controlled_buffer_88_out, xor_22_out);
  xor xor_15 (xor_15_out, controlled_buffer_90_out, xor_23_out);
  assign controlled_buffer_41_out = and_25_out ? d_ff_9_q : 1'bz;  // Controlled_Buffer controlled_buffer_41
  assign controlled_buffer_42_out = and_29_out ? d_ff_9_q : 1'bz;  // Controlled_Buffer controlled_buffer_42
  assign controlled_buffer_43_out = and_25_out ? d_ff_10_q : 1'bz;  // Controlled_Buffer controlled_buffer_43
  assign controlled_buffer_44_out = and_29_out ? d_ff_10_q : 1'bz;  // Controlled_Buffer controlled_buffer_44
  assign controlled_buffer_45_out = and_25_out ? d_ff_11_q : 1'bz;  // Controlled_Buffer controlled_buffer_45
  assign controlled_buffer_46_out = and_29_out ? d_ff_11_q : 1'bz;  // Controlled_Buffer controlled_buffer_46
  assign controlled_buffer_47_out = and_25_out ? d_ff_12_q : 1'bz;  // Controlled_Buffer controlled_buffer_47
  assign controlled_buffer_48_out = and_29_out ? d_ff_12_q : 1'bz;  // Controlled_Buffer controlled_buffer_48
  assign controlled_buffer_49_out = and_25_out ? d_ff_13_q : 1'bz;  // Controlled_Buffer controlled_buffer_49
  assign controlled_buffer_50_out = and_29_out ? d_ff_13_q : 1'bz;  // Controlled_Buffer controlled_buffer_50
  assign controlled_buffer_51_out = and_25_out ? d_ff_14_q : 1'bz;  // Controlled_Buffer controlled_buffer_51
  assign controlled_buffer_52_out = and_29_out ? d_ff_14_q : 1'bz;  // Controlled_Buffer controlled_buffer_52
  assign controlled_buffer_53_out = and_25_out ? d_ff_15_q : 1'bz;  // Controlled_Buffer controlled_buffer_53
  assign controlled_buffer_54_out = and_29_out ? d_ff_15_q : 1'bz;  // Controlled_Buffer controlled_buffer_54
  assign controlled_buffer_55_out = and_25_out ? d_ff_16_q : 1'bz;  // Controlled_Buffer controlled_buffer_55
  assign controlled_buffer_56_out = and_29_out ? d_ff_16_q : 1'bz;  // Controlled_Buffer controlled_buffer_56
  assign controlled_buffer_41_out = and_26_out ? d_ff_17_q : 1'bz;  // Controlled_Buffer controlled_buffer_57
  assign controlled_buffer_42_out = and_30_out ? d_ff_17_q : 1'bz;  // Controlled_Buffer controlled_buffer_58
  assign controlled_buffer_43_out = and_26_out ? d_ff_18_q : 1'bz;  // Controlled_Buffer controlled_buffer_59
  assign controlled_buffer_44_out = and_30_out ? d_ff_18_q : 1'bz;  // Controlled_Buffer controlled_buffer_60
  assign controlled_buffer_45_out = and_26_out ? d_ff_19_q : 1'bz;  // Controlled_Buffer controlled_buffer_61
  assign controlled_buffer_46_out = and_30_out ? d_ff_19_q : 1'bz;  // Controlled_Buffer controlled_buffer_62
  assign controlled_buffer_47_out = and_26_out ? d_ff_20_q : 1'bz;  // Controlled_Buffer controlled_buffer_63
  assign controlled_buffer_48_out = and_30_out ? d_ff_20_q : 1'bz;  // Controlled_Buffer controlled_buffer_64
  assign controlled_buffer_49_out = and_26_out ? d_ff_21_q : 1'bz;  // Controlled_Buffer controlled_buffer_65
  assign controlled_buffer_50_out = and_30_out ? d_ff_21_q : 1'bz;  // Controlled_Buffer controlled_buffer_66
  assign controlled_buffer_51_out = and_26_out ? d_ff_22_q : 1'bz;  // Controlled_Buffer controlled_buffer_67
  assign controlled_buffer_52_out = and_30_out ? d_ff_22_q : 1'bz;  // Controlled_Buffer controlled_buffer_68
  assign controlled_buffer_53_out = and_26_out ? d_ff_23_q : 1'bz;  // Controlled_Buffer controlled_buffer_69
  assign controlled_buffer_54_out = and_30_out ? d_ff_23_q : 1'bz;  // Controlled_Buffer controlled_buffer_70
  assign controlled_buffer_55_out = and_26_out ? d_ff_24_q : 1'bz;  // Controlled_Buffer controlled_buffer_71
  assign controlled_buffer_56_out = and_30_out ? d_ff_24_q : 1'bz;  // Controlled_Buffer controlled_buffer_72
  ROM #(.dataWidth(16)) rom_1 (.addr(d_ff_8_q), .data(rom_1_data));  // open: sel
  and and_36 (and_36_out, rom_1_data[10], rom_1_data[13]);
  and and_37 (and_37_out, rom_1_data[11], rom_1_data[10], rom_1_data[12]);
  and and_38 (and_38_out, ~rom_1_data[11], ~rom_1_data[10], rom_1_data[12]);  // AND_Gate
  xor xor_16 (xor_16_out, rom_1_data[12], rom_1_data[13]);
  and and_39 (and_39_out, rom_1_data[15], ~rom_1_data[14]);  // AND_Gate
  and and_40 (and_40_out, ~rom_1_data[13], and_62_out);  // AND_Gate
  and and_41 (and_41_out, rom_1_data[11], ~and_40_out);  // AND_Gate
  and and_42 (and_42_out, rom_1_data[12], rom_1_data[13]);
  and and_43 (and_43_out, ~and_42_out, and_62_out);  // AND_Gate
  xor xor_17 (xor_17_out, controlled_buffer_74_out, or_1_out);
  or or_1 (or_1_out, and_45_out, and_44_out);
  and and_44 (and_44_out, controlled_buffer_83_out, or_2_out);
  and and_45 (and_45_out, xor_18_out, controlled_buffer_76_out);
  xor xor_18 (xor_18_out, controlled_buffer_83_out, or_2_out);
  or or_2 (or_2_out, and_46_out, and_47_out);
  and and_46 (and_46_out, xor_19_out, controlled_buffer_78_out);
  and and_47 (and_47_out, controlled_buffer_82_out, or_3_out);
  xor xor_19 (xor_19_out, controlled_buffer_82_out, or_3_out);
  or or_3 (or_3_out, and_48_out, and_49_out);
  and and_48 (and_48_out, xor_20_out, controlled_buffer_77_out);
  and and_49 (and_49_out, controlled_buffer_95_out, or_4_out);
  xor xor_20 (xor_20_out, controlled_buffer_95_out, or_4_out);
  or or_4 (or_4_out, and_51_out, and_50_out);
  and and_50 (and_50_out, controlled_buffer_94_out, or_5_out);
  and and_51 (and_51_out, xor_21_out, controlled_buffer_79_out);
  xor xor_21 (xor_21_out, controlled_buffer_94_out, or_5_out);
  or or_5 (or_5_out, and_53_out, and_52_out);
  and and_52 (and_52_out, controlled_buffer_107_out, or_6_out);
  and and_53 (and_53_out, xor_22_out, controlled_buffer_88_out);
  xor xor_22 (xor_22_out, controlled_buffer_107_out, or_6_out);
  or or_6 (or_6_out, and_54_out, and_55_out);
  and and_54 (and_54_out, xor_23_out, controlled_buffer_90_out);
  and and_55 (and_55_out, controlled_buffer_106_out, and_56_out);
  xor xor_23 (xor_23_out, controlled_buffer_106_out, and_56_out);
  and and_56 (and_56_out, controlled_buffer_89_out, controlled_buffer_122_out);
  xor xor_24 (xor_24_out, controlled_buffer_89_out, controlled_buffer_122_out);
  and and_57 (and_57_out, rom_1_data[15], rom_1_data[14], ~rom_1_data[13], ~rom_1_data[12]);  // AND_Gate
  or or_7 (or_7_out, and_36_out, and_37_out, and_38_out);
  and and_58 (and_58_out, or_7_out, and_61_out);
  and and_59 (and_59_out, rom_1_data[11], and_61_out);
  and and_60 (and_60_out, rom_1_data[13], and_61_out);
  and and_61 (and_61_out, xor_16_out, ~rom_1_data[15], ~rom_1_data[14]);  // AND_Gate
  and and_62 (and_62_out, ~rom_1_data[15], rom_1_data[14]);  // AND_Gate
  xnor xnor_1 (xnor_1_out, rom_1_data[15], rom_1_data[14]);
  and and_63 (and_63_out, and_62_out, rom_1_data[13], rom_1_data[12]);
  assign controlled_buffer_73_out = and_43_out ? d_ff_8_q[7] : 1'bz;  // Controlled_Buffer controlled_buffer_73
  and and_64 (and_64_out, and_43_out, and_41_out);
  and and_65 (and_65_out, ~and_41_out, and_63_out);  // AND_Gate
  or or_8 (or_8_out, and_65_out, xnor_1_out);
  or or_9 (or_9_out, and_39_out, or_8_out, and_63_out);
  assign controlled_buffer_74_out = and_64_out ? and_69_out : 1'bz;  // Controlled_Buffer controlled_buffer_74
  not not_7 (not_7_out, or_8_out);
  assign controlled_buffer_75_out = not_8_out ? controlled_buffer_41_out : 1'bz;  // Controlled_Buffer controlled_buffer_75
  not not_8 (not_8_out, and_39_out);
  and and_66 (and_66_out, rom_1_data[11], and_40_out);
  and and_67 (and_67_out, ~rom_1_data[12], and_40_out);  // AND_Gate
  assign controlled_buffer_76_out = and_43_out ? d_ff_8_q[6] : 1'bz;  // Controlled_Buffer controlled_buffer_76
  assign controlled_buffer_77_out = and_43_out ? d_ff_8_q[4] : 1'bz;  // Controlled_Buffer controlled_buffer_77
  assign controlled_buffer_78_out = and_43_out ? d_ff_8_q[5] : 1'bz;  // Controlled_Buffer controlled_buffer_78
  assign controlled_buffer_79_out = and_43_out ? d_ff_8_q[3] : 1'bz;  // Controlled_Buffer controlled_buffer_79
  assign controlled_buffer_76_out = or_9_out ? and_68_out : 1'bz;  // Controlled_Buffer controlled_buffer_80
  assign controlled_buffer_73_out = or_9_out ? and_69_out : 1'bz;  // Controlled_Buffer controlled_buffer_81
  assign controlled_buffer_82_out = and_64_out ? and_71_out : 1'bz;  // Controlled_Buffer controlled_buffer_82
  assign controlled_buffer_83_out = and_64_out ? and_68_out : 1'bz;  // Controlled_Buffer controlled_buffer_83
  and and_68 (and_68_out, controlled_buffer_85_out, not_7_out);
  and and_69 (and_69_out, controlled_buffer_75_out, not_7_out);
  assign controlled_buffer_75_out = and_39_out ? controlled_buffer_42_out : 1'bz;  // Controlled_Buffer controlled_buffer_84
  assign controlled_buffer_85_out = and_39_out ? controlled_buffer_44_out : 1'bz;  // Controlled_Buffer controlled_buffer_85
  assign controlled_buffer_85_out = not_8_out ? controlled_buffer_43_out : 1'bz;  // Controlled_Buffer controlled_buffer_86
  assign controlled_buffer_87_out = not_8_out ? controlled_buffer_45_out : 1'bz;  // Controlled_Buffer controlled_buffer_87
  or or_10 (or_10_out, and_58_out, and_66_out);
  or or_11 (or_11_out, and_59_out, and_67_out);
  assign controlled_buffer_88_out = and_43_out ? d_ff_8_q[2] : 1'bz;  // Controlled_Buffer controlled_buffer_88
  assign controlled_buffer_89_out = and_43_out ? d_ff_8_q[0] : 1'bz;  // Controlled_Buffer controlled_buffer_89
  assign controlled_buffer_90_out = and_43_out ? d_ff_8_q[1] : 1'bz;  // Controlled_Buffer controlled_buffer_90
  assign controlled_buffer_74_out = or_12_out ? rom_1_data[7] : 1'bz;  // Controlled_Buffer controlled_buffer_91
  and and_70 (and_70_out, ~and_41_out, and_43_out);  // AND_Gate
  assign controlled_buffer_77_out = or_9_out ? and_72_out : 1'bz;  // Controlled_Buffer controlled_buffer_92
  assign controlled_buffer_78_out = or_9_out ? and_71_out : 1'bz;  // Controlled_Buffer controlled_buffer_93
  assign controlled_buffer_94_out = and_64_out ? and_74_out : 1'bz;  // Controlled_Buffer controlled_buffer_94
  assign controlled_buffer_95_out = and_64_out ? and_72_out : 1'bz;  // Controlled_Buffer controlled_buffer_95
  and and_71 (and_71_out, controlled_buffer_87_out, not_7_out);
  and and_72 (and_72_out, controlled_buffer_96_out, not_7_out);
  assign controlled_buffer_96_out = and_39_out ? controlled_buffer_48_out : 1'bz;  // Controlled_Buffer controlled_buffer_96
  assign controlled_buffer_87_out = and_39_out ? controlled_buffer_46_out : 1'bz;  // Controlled_Buffer controlled_buffer_97
  assign controlled_buffer_98_out = not_8_out ? controlled_buffer_49_out : 1'bz;  // Controlled_Buffer controlled_buffer_98
  assign controlled_buffer_96_out = not_8_out ? controlled_buffer_47_out : 1'bz;  // Controlled_Buffer controlled_buffer_99
  assign controlled_buffer_82_out = or_12_out ? rom_1_data[5] : 1'bz;  // Controlled_Buffer controlled_buffer_100
  assign controlled_buffer_83_out = or_12_out ? rom_1_data[6] : 1'bz;  // Controlled_Buffer controlled_buffer_101
  assign controlled_buffer_95_out = or_12_out ? rom_1_data[4] : 1'bz;  // Controlled_Buffer controlled_buffer_102
  assign controlled_buffer_94_out = or_12_out ? rom_1_data[3] : 1'bz;  // Controlled_Buffer controlled_buffer_103
  or or_12 (or_12_out, xnor_1_out, and_39_out, and_63_out, and_70_out);
  assign controlled_buffer_88_out = or_9_out ? and_73_out : 1'bz;  // Controlled_Buffer controlled_buffer_104
  assign controlled_buffer_79_out = or_9_out ? and_74_out : 1'bz;  // Controlled_Buffer controlled_buffer_105
  assign controlled_buffer_106_out = and_64_out ? and_76_out : 1'bz;  // Controlled_Buffer controlled_buffer_106
  assign controlled_buffer_107_out = and_64_out ? and_73_out : 1'bz;  // Controlled_Buffer controlled_buffer_107
  and and_73 (and_73_out, controlled_buffer_109_out, not_7_out);
  and and_74 (and_74_out, controlled_buffer_98_out, not_7_out);
  assign controlled_buffer_98_out = and_39_out ? controlled_buffer_50_out : 1'bz;  // Controlled_Buffer controlled_buffer_108
  assign controlled_buffer_109_out = and_39_out ? controlled_buffer_52_out : 1'bz;  // Controlled_Buffer controlled_buffer_109
  assign controlled_buffer_110_out = not_8_out ? controlled_buffer_53_out : 1'bz;  // Controlled_Buffer controlled_buffer_110
  assign controlled_buffer_109_out = not_8_out ? controlled_buffer_51_out : 1'bz;  // Controlled_Buffer controlled_buffer_111
  D_Flip_Flop d_ff_25 (
    .clk(and_19_out), .D(controlled_buffer_21_out), .Q(d_ff_25_q), .reset(not_3_out));  // open: Qn, preset, en
  D_Flip_Flop d_ff_26 (
    .clk(and_19_out), .D(controlled_buffer_22_out), .Q(d_ff_26_q), .reset(not_3_out));  // open: Qn, preset, en
  D_Flip_Flop d_ff_27 (
    .clk(and_19_out), .D(controlled_buffer_23_out), .Q(d_ff_27_q), .reset(not_3_out));  // open: Qn, preset, en
  D_Flip_Flop d_ff_28 (
    .clk(and_19_out), .D(controlled_buffer_24_out), .Q(d_ff_28_q), .reset(not_3_out));  // open: Qn, preset, en
  D_Flip_Flop d_ff_29 (
    .clk(and_19_out), .D(controlled_buffer_25_out), .Q(d_ff_29_q), .reset(not_3_out));  // open: Qn, preset, en
  D_Flip_Flop d_ff_30 (
    .clk(and_19_out), .D(controlled_buffer_26_out), .Q(d_ff_30_q), .reset(not_3_out));  // open: Qn, preset, en
  D_Flip_Flop d_ff_31 (
    .clk(and_19_out), .D(controlled_buffer_27_out), .Q(d_ff_31_q), .reset(not_3_out));  // open: Qn, preset, en
  D_Flip_Flop d_ff_32 (
    .clk(and_19_out), .D(controlled_buffer_28_out), .Q(d_ff_32_q), .reset(not_3_out));  // open: Qn, preset, en
  assign controlled_buffer_41_out = and_24_out ? d_ff_33_q : 1'bz;  // Controlled_Buffer controlled_buffer_112
  D_Flip_Flop d_ff_33 (
    .clk(and_20_out), .D(controlled_buffer_21_out), .Q(d_ff_33_q), .reset(not_3_out));  // open: Qn, preset, en
  assign controlled_buffer_43_out = and_24_out ? d_ff_34_q : 1'bz;  // Controlled_Buffer controlled_buffer_113
  D_Flip_Flop d_ff_34 (
    .clk(and_20_out), .D(controlled_buffer_22_out), .Q(d_ff_34_q), .reset(not_3_out));  // open: Qn, preset, en
  D_Flip_Flop d_ff_35 (
    .clk(and_20_out), .D(controlled_buffer_23_out), .Q(d_ff_35_q), .reset(not_3_out));  // open: Qn, preset, en
  assign controlled_buffer_45_out = and_24_out ? d_ff_35_q : 1'bz;  // Controlled_Buffer controlled_buffer_114
  D_Flip_Flop d_ff_36 (
    .clk(and_20_out), .D(controlled_buffer_24_out), .Q(d_ff_36_q), .reset(not_3_out));  // open: Qn, preset, en
  assign controlled_buffer_47_out = and_24_out ? d_ff_36_q : 1'bz;  // Controlled_Buffer controlled_buffer_115
  D_Flip_Flop d_ff_37 (
    .clk(and_20_out), .D(controlled_buffer_25_out), .Q(d_ff_37_q), .reset(not_3_out));  // open: Qn, preset, en
  assign controlled_buffer_49_out = and_24_out ? d_ff_37_q : 1'bz;  // Controlled_Buffer controlled_buffer_116
  assign controlled_buffer_51_out = and_24_out ? d_ff_38_q : 1'bz;  // Controlled_Buffer controlled_buffer_117
  D_Flip_Flop d_ff_38 (
    .clk(and_20_out), .D(controlled_buffer_26_out), .Q(d_ff_38_q), .reset(not_3_out));  // open: Qn, preset, en
  D_Flip_Flop d_ff_39 (
    .clk(and_20_out), .D(controlled_buffer_27_out), .Q(d_ff_39_q), .reset(not_3_out));  // open: Qn, preset, en
  assign controlled_buffer_53_out = and_24_out ? d_ff_39_q : 1'bz;  // Controlled_Buffer controlled_buffer_118
  assign controlled_buffer_55_out = and_24_out ? d_ff_40_q : 1'bz;  // Controlled_Buffer controlled_buffer_119
  D_Flip_Flop d_ff_40 (
    .clk(and_20_out), .D(controlled_buffer_28_out), .Q(d_ff_40_q), .reset(not_3_out));  // open: Qn, preset, en
  assign controlled_buffer_107_out = or_12_out ? rom_1_data[2] : 1'bz;  // Controlled_Buffer controlled_buffer_120
  assign controlled_buffer_106_out = or_12_out ? rom_1_data[1] : 1'bz;  // Controlled_Buffer controlled_buffer_121
  assign controlled_buffer_122_out = or_12_out ? rom_1_data[0] : 1'bz;  // Controlled_Buffer controlled_buffer_122
  assign controlled_buffer_90_out = or_9_out ? and_76_out : 1'bz;  // Controlled_Buffer controlled_buffer_123
  assign controlled_buffer_89_out = or_9_out ? and_75_out : 1'bz;  // Controlled_Buffer controlled_buffer_124
  assign controlled_buffer_122_out = and_64_out ? and_75_out : 1'bz;  // Controlled_Buffer controlled_buffer_125
  and and_75 (and_75_out, controlled_buffer_127_out, not_7_out);
  and and_76 (and_76_out, controlled_buffer_110_out, not_7_out);
  assign controlled_buffer_110_out = and_39_out ? controlled_buffer_54_out : 1'bz;  // Controlled_Buffer controlled_buffer_126
  assign controlled_buffer_127_out = and_39_out ? controlled_buffer_56_out : 1'bz;  // Controlled_Buffer controlled_buffer_127
  assign controlled_buffer_127_out = not_8_out ? controlled_buffer_55_out : 1'bz;  // Controlled_Buffer controlled_buffer_128
  assign controlled_buffer_41_out = and_23_out ? d_ff_25_q : 1'bz;  // Controlled_Buffer controlled_buffer_129
  assign controlled_buffer_42_out = and_27_out ? d_ff_25_q : 1'bz;  // Controlled_Buffer controlled_buffer_130
  assign controlled_buffer_43_out = and_23_out ? d_ff_26_q : 1'bz;  // Controlled_Buffer controlled_buffer_131
  assign controlled_buffer_44_out = and_27_out ? d_ff_26_q : 1'bz;  // Controlled_Buffer controlled_buffer_132
  assign controlled_buffer_45_out = and_23_out ? d_ff_27_q : 1'bz;  // Controlled_Buffer controlled_buffer_133
  assign controlled_buffer_46_out = and_27_out ? d_ff_27_q : 1'bz;  // Controlled_Buffer controlled_buffer_134
  assign controlled_buffer_47_out = and_23_out ? d_ff_28_q : 1'bz;  // Controlled_Buffer controlled_buffer_135
  assign controlled_buffer_48_out = and_27_out ? d_ff_28_q : 1'bz;  // Controlled_Buffer controlled_buffer_136
  assign controlled_buffer_49_out = and_23_out ? d_ff_29_q : 1'bz;  // Controlled_Buffer controlled_buffer_137
  assign controlled_buffer_50_out = and_27_out ? d_ff_29_q : 1'bz;  // Controlled_Buffer controlled_buffer_138
  assign controlled_buffer_51_out = and_23_out ? d_ff_30_q : 1'bz;  // Controlled_Buffer controlled_buffer_139
  assign controlled_buffer_52_out = and_27_out ? d_ff_30_q : 1'bz;  // Controlled_Buffer controlled_buffer_140
  assign controlled_buffer_53_out = and_23_out ? d_ff_31_q : 1'bz;  // Controlled_Buffer controlled_buffer_141
  assign controlled_buffer_54_out = and_27_out ? d_ff_31_q : 1'bz;  // Controlled_Buffer controlled_buffer_142
  assign controlled_buffer_55_out = and_23_out ? d_ff_32_q : 1'bz;  // Controlled_Buffer controlled_buffer_143
  assign controlled_buffer_56_out = and_27_out ? d_ff_32_q : 1'bz;  // Controlled_Buffer controlled_buffer_144
  assign controlled_buffer_42_out = and_28_out ? d_ff_33_q : 1'bz;  // Controlled_Buffer controlled_buffer_145
  assign controlled_buffer_44_out = and_28_out ? d_ff_34_q : 1'bz;  // Controlled_Buffer controlled_buffer_146
  assign controlled_buffer_46_out = and_28_out ? d_ff_35_q : 1'bz;  // Controlled_Buffer controlled_buffer_147
  assign controlled_buffer_48_out = and_28_out ? d_ff_36_q : 1'bz;  // Controlled_Buffer controlled_buffer_148
  assign controlled_buffer_50_out = and_28_out ? d_ff_37_q : 1'bz;  // Controlled_Buffer controlled_buffer_149
  assign controlled_buffer_52_out = and_28_out ? d_ff_38_q : 1'bz;  // Controlled_Buffer controlled_buffer_150
  assign controlled_buffer_54_out = and_28_out ? d_ff_39_q : 1'bz;  // Controlled_Buffer controlled_buffer_151
  assign controlled_buffer_56_out = and_28_out ? d_ff_40_q : 1'bz;  // Controlled_Buffer controlled_buffer_152
  or or_13 (or_13_out, and_60_out, and_40_out);
  assign controlled_buffer_153_out = and_61_out ? rom_1_data[7] : 1'bz;  // Controlled_Buffer controlled_buffer_153
  assign controlled_buffer_154_out = and_61_out ? rom_1_data[6] : 1'bz;  // Controlled_Buffer controlled_buffer_154
  assign controlled_buffer_155_out = and_61_out ? rom_1_data[5] : 1'bz;  // Controlled_Buffer controlled_buffer_155
  not not_9 (not_9_out, and_61_out);
  assign controlled_buffer_155_out = not_9_out ? controlled_buffer_46_out : 1'bz;  // Controlled_Buffer controlled_buffer_156
  assign controlled_buffer_154_out = not_9_out ? controlled_buffer_44_out : 1'bz;  // Controlled_Buffer controlled_buffer_157
  assign controlled_buffer_153_out = not_9_out ? controlled_buffer_42_out : 1'bz;  // Controlled_Buffer controlled_buffer_158
  assign controlled_buffer_159_out = and_61_out ? rom_1_data[1] : 1'bz;  // Controlled_Buffer controlled_buffer_159
  assign controlled_buffer_160_out = and_61_out ? rom_1_data[4] : 1'bz;  // Controlled_Buffer controlled_buffer_160
  assign controlled_buffer_161_out = and_61_out ? rom_1_data[2] : 1'bz;  // Controlled_Buffer controlled_buffer_161
  assign controlled_buffer_162_out = and_61_out ? rom_1_data[3] : 1'bz;  // Controlled_Buffer controlled_buffer_162
  assign controlled_buffer_162_out = not_9_out ? controlled_buffer_50_out : 1'bz;  // Controlled_Buffer controlled_buffer_163
  assign controlled_buffer_160_out = not_9_out ? controlled_buffer_48_out : 1'bz;  // Controlled_Buffer controlled_buffer_164
  assign controlled_buffer_159_out = not_9_out ? controlled_buffer_54_out : 1'bz;  // Controlled_Buffer controlled_buffer_165
  assign controlled_buffer_161_out = not_9_out ? controlled_buffer_52_out : 1'bz;  // Controlled_Buffer controlled_buffer_166
  and and_77 (and_77_out, and_57_out, rom_1_data[0]);
  and and_78 (and_78_out, and_57_out, rom_1_data[1]);
  and and_79 (and_79_out, and_57_out, rom_1_data[2]);
  and and_80 (and_80_out, and_57_out, rom_1_data[3]);
  and and_81 (and_81_out, and_57_out, rom_1_data[4]);
  and and_82 (and_82_out, and_57_out, rom_1_data[5]);
  and and_83 (and_83_out, and_57_out, rom_1_data[6]);
  and and_84 (and_84_out, and_57_out, rom_1_data[7]);
  assign controlled_buffer_167_out = and_61_out ? rom_1_data[0] : 1'bz;  // Controlled_Buffer controlled_buffer_167
  and and_85 (and_85_out, not_10_out, controlled_buffer_153_out);
  and and_86 (and_86_out, not_10_out, controlled_buffer_154_out);
  and and_87 (and_87_out, not_10_out, controlled_buffer_155_out);
  and and_88 (and_88_out, not_10_out, controlled_buffer_160_out);
  and and_89 (and_89_out, controlled_buffer_162_out, not_10_out);
  and and_90 (and_90_out, controlled_buffer_161_out, not_10_out);
  and and_91 (and_91_out, controlled_buffer_159_out, not_10_out);
  and and_92 (and_92_out, controlled_buffer_167_out, not_10_out);
  assign controlled_buffer_167_out = not_9_out ? controlled_buffer_56_out : 1'bz;  // Controlled_Buffer controlled_buffer_168
  not not_10 (not_10_out, and_40_out);
  not not_11 (not_11_out, and_101_out);
  and and_93 (and_93_out, controlled_buffer_41_out, not_11_out);
  and and_94 (and_94_out, controlled_buffer_43_out, not_11_out);
  and and_95 (and_95_out, controlled_buffer_45_out, not_11_out);
  and and_96 (and_96_out, controlled_buffer_47_out, not_11_out);
  and and_97 (and_97_out, controlled_buffer_49_out, not_11_out);
  and and_98 (and_98_out, controlled_buffer_51_out, not_11_out);
  and and_99 (and_99_out, controlled_buffer_53_out, not_11_out);
  and and_100 (and_100_out, controlled_buffer_55_out, not_11_out);
  or or_14 (or_14_out, and_77_out, or_10_out);
  or or_15 (or_15_out, and_78_out, or_11_out);
  or or_16 (or_16_out, and_80_out, or_13_out);
  or or_17 (or_17_out, and_81_out, or_13_out);
  and and_101 (and_101_out, ~or_17_out, ~or_16_out, ~and_79_out, ~or_15_out, or_14_out);  // AND_Gate
  xor xor_25 (xor_25_out, and_85_out, or_21_out);
  or or_18 (or_18_out, and_103_out, and_104_out);
  xor xor_26 (xor_26_out, xor_25_out, or_18_out);
  xor xor_27 (xor_27_out, and_93_out, xor_26_out);
  and and_102 (and_102_out, xor_27_out, or_23_out);
  assign controlled_buffer_21_out = and_143_out ? and_102_out : 1'bz;  // Controlled_Buffer controlled_buffer_169
  xor xor_28 (xor_28_out, and_86_out, or_21_out);
  and and_103 (and_103_out, or_19_out, xor_28_out);
  or or_19 (or_19_out, and_107_out, and_108_out);
  and and_104 (and_104_out, and_94_out, xor_29_out);
  xor xor_29 (xor_29_out, xor_28_out, or_19_out);
  xor xor_30 (xor_30_out, and_94_out, xor_29_out);
  and and_105 (and_105_out, xor_30_out, or_23_out);
  assign controlled_buffer_22_out = and_143_out ? and_105_out : 1'bz;  // Controlled_Buffer controlled_buffer_170
  and and_106 (and_106_out, or_17_out, ~or_16_out, and_110_out);  // AND_Gate
  and and_107 (and_107_out, or_24_out, xor_32_out);
  and and_108 (and_108_out, and_95_out, xor_33_out);
  xor xor_31 (xor_31_out, and_95_out, xor_33_out);
  and and_109 (and_109_out, ~or_17_out, ~or_16_out, ~and_79_out, or_15_out);  // AND_Gate
  and and_110 (and_110_out, and_79_out, or_15_out);
  or or_20 (or_20_out, and_106_out, and_116_out);
  and and_111 (and_111_out, or_14_out, and_115_out);
  or or_21 (or_21_out, or_20_out, and_115_out);
  or or_22 (or_22_out, or_20_out, and_111_out);
  or or_23 (or_23_out, and_101_out, and_109_out);
  xor xor_32 (xor_32_out, and_87_out, or_21_out);
  and and_112 (and_112_out, or_26_out, xor_34_out);
  or or_24 (or_24_out, and_112_out, and_113_out);
  and and_113 (and_113_out, and_96_out, xor_35_out);
  xor xor_33 (xor_33_out, xor_32_out, or_24_out);
  and and_114 (and_114_out, xor_31_out, or_23_out);
  assign controlled_buffer_23_out = and_143_out ? and_114_out : 1'bz;  // Controlled_Buffer controlled_buffer_171
  and and_115 (and_115_out, or_17_out, or_16_out, ~and_79_out);  // AND_Gate
  and and_116 (and_116_out, and_109_out, or_14_out);
  and and_117 (and_117_out, and_115_out, xnor_2_out);
  or or_25 (or_25_out, or_23_out, and_106_out, and_115_out);
  xor xor_34 (xor_34_out, and_88_out, or_21_out);
  and and_118 (and_118_out, or_27_out, xor_37_out);
  or or_26 (or_26_out, and_118_out, and_119_out);
  and and_119 (and_119_out, and_97_out, xor_38_out);
  xor xor_35 (xor_35_out, xor_34_out, or_26_out);
  xor xor_36 (xor_36_out, and_96_out, xor_35_out);
  and and_120 (and_120_out, xor_36_out, or_23_out);
  assign controlled_buffer_24_out = and_143_out ? and_120_out : 1'bz;  // Controlled_Buffer controlled_buffer_172
  and and_121 (and_121_out, or_17_out, ~or_16_out);  // AND_Gate
  and and_122 (and_122_out, ~and_110_out, and_121_out);  // AND_Gate
  xnor xnor_2 (xnor_2_out, or_15_out, or_14_out);
  xor xor_37 (xor_37_out, and_89_out, or_21_out);
  or or_27 (or_27_out, and_128_out, and_129_out);
  xor xor_38 (xor_38_out, xor_37_out, or_27_out);
  xor xor_39 (xor_39_out, and_97_out, xor_38_out);
  and and_123 (and_123_out, xor_39_out, or_23_out);
  assign controlled_buffer_25_out = and_143_out ? and_123_out : 1'bz;  // Controlled_Buffer controlled_buffer_173
  and and_124 (and_124_out, and_79_out, ~or_15_out);  // AND_Gate
  and and_125 (and_125_out, ~and_79_out, or_15_out);  // AND_Gate
  and and_126 (and_126_out, and_124_out, and_84_out);
  or or_28 (or_28_out, and_126_out, and_125_out);
  and and_127 (and_127_out, and_121_out, or_28_out);
  xor xor_40 (xor_40_out, and_90_out, or_21_out);
  and and_128 (and_128_out, or_29_out, xor_40_out);
  or or_29 (or_29_out, and_135_out, and_136_out);
  and and_129 (and_129_out, and_98_out, xor_41_out);
  xor xor_41 (xor_41_out, xor_40_out, or_29_out);
  xor xor_42 (xor_42_out, and_98_out, xor_41_out);
  and and_130 (and_130_out, xor_42_out, or_23_out);
  assign controlled_buffer_26_out = and_143_out ? and_130_out : 1'bz;  // Controlled_Buffer controlled_buffer_174
  and and_131 (and_131_out, ~and_79_out, ~or_14_out);  // AND_Gate
  and and_132 (and_132_out, ~and_79_out, or_14_out);  // AND_Gate
  or or_30 (or_30_out, and_124_out, and_132_out);
  or or_31 (or_31_out, and_124_out, and_131_out);
  and and_133 (and_133_out, and_121_out, or_30_out);
  and and_134 (and_134_out, and_121_out, or_31_out);
  and and_135 (and_135_out, or_33_out, xor_44_out);
  and and_136 (and_136_out, and_99_out, xor_45_out);
  xor xor_43 (xor_43_out, and_99_out, xor_45_out);
  or or_32 (or_32_out, xor_27_out, xor_43_out, xor_49_out, xor_42_out, xor_39_out, xor_36_out, xor_31_out, xor_30_out);
  and and_137 (and_137_out, or_23_out, xor_43_out);
  assign controlled_buffer_27_out = and_143_out ? and_137_out : 1'bz;  // Controlled_Buffer controlled_buffer_175
  xor xor_44 (xor_44_out, and_91_out, or_21_out);
  and and_138 (and_138_out, or_22_out, xor_47_out);
  or or_33 (or_33_out, and_138_out, and_139_out);
  and and_139 (and_139_out, and_100_out, xor_48_out);
  xor xor_45 (xor_45_out, xor_44_out, or_33_out);
  and and_140 (and_140_out, xor_27_out, and_115_out);
  and and_141 (and_141_out, or_32_out, ~and_115_out);  // AND_Gate
  or or_34 (or_34_out, and_141_out, and_140_out);
  xor xor_46 (xor_46_out, or_34_out, and_117_out);
  and and_142 (and_142_out, ~or_23_out, xor_46_out);  // AND_Gate
  and and_143 (and_143_out, ~and_40_out, or_25_out);  // AND_Gate
  or or_35 (or_35_out, and_142_out, and_144_out);
  assign controlled_buffer_28_out = and_143_out ? or_35_out : 1'bz;  // Controlled_Buffer controlled_buffer_176
  xor xor_47 (xor_47_out, and_92_out, or_21_out);
  xor xor_48 (xor_48_out, xor_47_out, or_22_out);
  xor xor_49 (xor_49_out, and_100_out, xor_48_out);
  and and_144 (and_144_out, or_23_out, xor_49_out);
  and and_145 (and_145_out, ~and_93_out, or_36_out);  // AND_Gate
  and and_146 (and_146_out, and_145_out, and_147_out, ~and_133_out, and_134_out);  // AND_Gate
  assign controlled_buffer_177_out = and_122_out ? 1'b0 : 1'bz;  // Controlled_Buffer controlled_buffer_177
  buf buffer_1 (controlled_buffer_21_out, controlled_buffer_177_out);
  buf buffer_2 (controlled_buffer_22_out, controlled_buffer_177_out);
  buf buffer_3 (controlled_buffer_23_out, controlled_buffer_177_out);
  buf buffer_4 (controlled_buffer_24_out, controlled_buffer_177_out);
  buf buffer_5 (controlled_buffer_25_out, controlled_buffer_177_out);
  buf buffer_6 (controlled_buffer_26_out, controlled_buffer_177_out);
  buf buffer_7 (controlled_buffer_27_out, controlled_buffer_177_out);
  or or_36 (or_36_out, and_94_out, and_95_out, and_96_out, and_97_out, and_98_out, and_99_out, and_100_out);
  and and_147 (and_147_out, ~and_85_out, or_39_out);  // AND_Gate
  or or_37 (or_37_out, and_147_out, and_145_out);
  and and_148 (and_148_out, ~and_134_out, and_133_out, or_37_out);  // AND_Gate
  and and_149 (and_149_out, and_133_out, and_134_out, xor_51_out);
  or or_38 (or_38_out, and_146_out, and_148_out, and_149_out);
  xor xor_50 (xor_50_out, and_127_out, or_38_out);
  assign controlled_buffer_28_out = and_122_out ? xor_50_out : 1'bz;  // Controlled_Buffer controlled_buffer_178
  or or_39 (or_39_out, and_86_out, and_87_out, and_88_out, and_89_out, and_90_out, and_91_out, and_92_out);
  xor xor_51 (xor_51_out, and_147_out, and_145_out);

  // Notes on the sheet:
  //   source
  //   target
  //   write
  //   contents of rom_1 (hex, n*v repeats v):
  //   0 0 0 1301 ce01 8800 89ff c419 5006 8800 98ff 9900 1e01 42f8 1b01 ce01 2610 42f3 f000
endmodule
